// Logisim project mainc.circ as structural Verilog: 14 circuits, main circuit GAME
module main (
  input  [7:0] birth,
  input  [7:0] survival,
  input  survival_cond__if_null,
  input  game_ON___OFF,
  input  creative__0____survival__1,
  input  clear_field,
  input  [2:0] ID_of_pattern,
  input  [3:0] zone_width,
  input  [6:0] cursor,
  output [31:0] stb_0,
  output [31:0] row_0,
  output [31:0] stb_1,
  output [31:0] row_1,
  output [31:0] stb_2,
  output [31:0] row_2,
  output [31:0] stb_3,
  output [31:0] row_3,
  output [31:0] stb_4,
  output [31:0] row_4,
  output [31:0] stb_5,
  output [31:0] row_5,
  output [31:0] stb_6,
  output [31:0] row_6,
  output clock,
  output [31:0] row_7,
  output out_26,
  output [31:0] row_8,
  output [31:0] row_9,
  output [31:0] row_10,
  output [31:0] row_11,
  output [31:0] row_12,
  output [31:0] row_13,
  output [31:0] row_14,
  output [31:0] row_15,
  output [31:0] row_16,
  output [31:0] row_17,
  output [31:0] row_18,
  output [31:0] row_19,
  output [31:0] row_20,
  output [31:0] row_21,
  output [31:0] row_22,
  output [31:0] row_23,
  output [31:0] row_24,
  output [31:0] row_25,
  output [31:0] row_26,
  output [31:0] row_27,
  output [31:0] row_28,
  output [31:0] row_29,
  output [31:0] row_30,
  output [31:0] row_31
);

  wire and_3_out, and_4_out, and_5_out, and_6_out, and_7_out, and_8_out, and_9_out, and_10_out, and_11_out,
       and_12_out, and_13_out, and_14_out, and_15_out, and_16_out, and_18_out, and_19_out, and_20_out,
       and_21_out, and_22_out, and_23_out, cdm_8e_1_p4, cdm_8e_1_p5, cell_state, change_cell_state,
       clear_field_STB, clear_field_t, code, comparator_1_eq, comparator_2_eq, comparator_3_eq,
       comparator_4_eq, comparator_5_eq, comparator_6_eq, comparator_6_gt, comparator_7_eq, comparator_7_lt,
       comparator_8_eq, comparator_9_eq, comparator_10_eq, comparator_11_eq, comparator_12_eq,
       comparator_13_eq, comparator_14_eq, comparator_15_eq, comparator_16_eq, comparator_17_eq,
       comparator_18_eq, comparator_19_eq, cursor_1_is_enter, data, death_cond__if_null, decoder_1_out0,
       decoder_1_out1, decoder_2_out1, decoder_4_out1, decoder_5_out1, decoder_7_out0, decoder_7_out1,
       decoder_8_out1, decoder_9_out1, decoder_11_out0, decoder_11_out1, decoder_13_out0, decoder_13_out1,
       decoder_14_out1, decoder_15_out1, decoder_16_out1, decoder_17_out1, decoder_18_out1, drow,
       drow_pattern, game_ON, I_Osel, In_out, is_row_null, mem, multiplexer_1_out, multiplexer_6_out,
       multiplexer_7_out, no_any_alive, not_1_out, not_2_out, not_3_out, not_4_out, not_5_out, not_6_out,
       not_7_out, not_8_out, not_9_out, not_10_out, not_11_out, or_1_out, or_2_out, or_3_out, or_4_out,
       or_5_out, or_6_out, or_7_out, or_8_out, or_9_out, or_10_out, RAM, show_result, update_fixed_buffer,
       wait_1_out_2, WIN___LOSE, xnor_1_out, xnor_2_out, xnor_3_out;
  wire [0:0] not_12_out;
  wire [3:0] counter_1_q;
  wire [4:0] curs_X, curs_Y, multiplexer_2_out, multiplexer_3_out, multiplexer_4_out, multiplexer_5_out, r_X,
       r_Y, X, Y;
  wire [6:0] cursor_t;
  wire [7:0] cdm_8e_1_p9, cdm_8e_1_p10, controlled_buffer_2_out, controlled_buffer_11_out,
       count_of_neighbors, I_Odata, not_13_out, register_2_q, register_3_q, register_5_q, register_8_q,
       register_9_q;
  wire [7:1] pull_resistor_3_node, pull_resistor_11_node, pull_resistor_21_node, pull_resistor_28_node,
       pull_resistor_40_node, register_6_q;
  wire [7:3] pull_resistor_35_node;
  wire [7:4] pull_resistor_47_node;
  wire [7:5] cdm_8e_1_p1, cdm_8e_1_p2, pull_resistor_10_node, pull_resistor_18_node, register_1_q,
       register_4_q;
  wire [15:0] I_Oadr;
  wire [31:0] converter_1_converted_row, cursor_visualization_1_row_0_2, cursor_visualization_1_row_1_2,
       cursor_visualization_1_row_2_2, cursor_visualization_1_row_3_2, cursor_visualization_1_row_4_2,
       cursor_visualization_1_row_5_2, cursor_visualization_1_row_6_2, cursor_visualization_1_row_7_2,
       cursor_visualization_1_row_8_2, cursor_visualization_1_row_9_2, cursor_visualization_1_row_10_2,
       cursor_visualization_1_row_11_2, cursor_visualization_1_row_12_2, cursor_visualization_1_row_13_2,
       cursor_visualization_1_row_14_2, cursor_visualization_1_row_15_2, cursor_visualization_1_row_16_2,
       cursor_visualization_1_row_17_2, cursor_visualization_1_row_18_2, cursor_visualization_1_row_19_2,
       cursor_visualization_1_row_20_2, cursor_visualization_1_row_21_2, cursor_visualization_1_row_22_2,
       cursor_visualization_1_row_23_2, cursor_visualization_1_row_24_2, cursor_visualization_1_row_25_2,
       cursor_visualization_1_row_26_2, cursor_visualization_1_row_27_2, cursor_visualization_1_row_28_2,
       cursor_visualization_1_row_29_2, cursor_visualization_1_row_30_2, cursor_visualization_1_row_31_2,
       fixed_buffer_1_row_0_2, fixed_buffer_1_row_1_2, fixed_buffer_1_row_2_2, fixed_buffer_1_row_3_2,
       fixed_buffer_1_row_4_2, fixed_buffer_1_row_5_2, fixed_buffer_1_row_6_2, fixed_buffer_1_row_7_2,
       fixed_buffer_1_row_8_2, fixed_buffer_1_row_9_2, fixed_buffer_1_row_10_2, fixed_buffer_1_row_11_2,
       fixed_buffer_1_row_12_2, fixed_buffer_1_row_13_2, fixed_buffer_1_row_14_2, fixed_buffer_1_row_15_2,
       fixed_buffer_1_row_16_2, fixed_buffer_1_row_17_2, fixed_buffer_1_row_18_2, fixed_buffer_1_row_19_2,
       fixed_buffer_1_row_20_2, fixed_buffer_1_row_21_2, fixed_buffer_1_row_22_2, fixed_buffer_1_row_23_2,
       fixed_buffer_1_row_24_2, fixed_buffer_1_row_25_2, fixed_buffer_1_row_26_2, fixed_buffer_1_row_27_2,
       fixed_buffer_1_row_28_2, fixed_buffer_1_row_29_2, fixed_buffer_1_row_30_2, fixed_buffer_1_row_31_2,
       write_buffer_1_row0, write_buffer_1_row0_2, write_buffer_1_row0_3, write_buffer_1_row0_4,
       write_buffer_1_row0_5, write_buffer_1_row0_6, write_buffer_1_row0_7, write_buffer_1_row0_8,
       write_buffer_1_row0_9, write_buffer_1_row0_10, write_buffer_1_row0_11, write_buffer_1_row0_12,
       write_buffer_1_row0_13, write_buffer_1_row0_14, write_buffer_1_row0_15, write_buffer_1_row0_16,
       write_buffer_1_row0_17, write_buffer_1_row1, write_buffer_1_row2, write_buffer_1_row3,
       write_buffer_1_row4, write_buffer_1_row5, write_buffer_1_row6, write_buffer_1_row7,
       write_buffer_1_row8, write_buffer_1_row9, write_buffer_1_row10, write_buffer_1_row11,
       write_buffer_1_row12, write_buffer_1_row13, write_buffer_1_row14, write_buffer_1_row15,
       zone_visualization_1_row_0_2, zone_visualization_1_row_1_2, zone_visualization_1_row_2_2,
       zone_visualization_1_row_3_2, zone_visualization_1_row_4_2, zone_visualization_1_row_5_2,
       zone_visualization_1_row_6_2, zone_visualization_1_row_7_2, zone_visualization_1_row_8_2,
       zone_visualization_1_row_9_2, zone_visualization_1_row_10_2, zone_visualization_1_row_11_2,
       zone_visualization_1_row_12_2, zone_visualization_1_row_13_2, zone_visualization_1_row_14_2,
       zone_visualization_1_row_15_2, zone_visualization_1_row_16_2, zone_visualization_1_row_17_2,
       zone_visualization_1_row_18_2, zone_visualization_1_row_19_2, zone_visualization_1_row_20_2,
       zone_visualization_1_row_21_2, zone_visualization_1_row_22_2, zone_visualization_1_row_23_2,
       zone_visualization_1_row_24_2, zone_visualization_1_row_25_2, zone_visualization_1_row_26_2,
       zone_visualization_1_row_27_2, zone_visualization_1_row_28_2, zone_visualization_1_row_29_2,
       zone_visualization_1_row_30_2, zone_visualization_1_row_31_2;

  and and_1 (I_Osel, not_1_out, clock, data);
  cursor cursor_1 (.ASCII_code(cursor_t), .X(curs_X), .Y(curs_Y), .is_enter(cursor_1_is_enter));
  // Probe on {cdm_8e_1_p1, r_Y}
  // Probe on {cdm_8e_1_p2, r_X}
  // Probe on cdm_8e_1_p4
  // Probe on nothing
  Clock clock_1 (.out(clock));
  not not_1 (not_1_out, not_2_out);
  and and_2 (RAM, not_2_out, data);
  Decoder #(.disabled(0)) decoder_1 (.out0(decoder_1_out0), .out1(decoder_1_out1), .sel(In_out), .en(and_4_out));
  // CdM_8e cdm_8e_1: pin names not known; wires that end beside it: {cdm_8e_1_p1, r_Y}, {cdm_8e_1_p2, r_X}, clock, cdm_8e_1_p4, cdm_8e_1_p5, mem, In_out, I_Oadr, cdm_8e_1_p9, cdm_8e_1_p10
  assign cdm_8e_1_p10 = In_out ? I_Odata : 8'bz;  // Controlled_Buffer controlled_buffer_1
  not not_2 (not_2_out, and_9_out);
  and and_3 (and_3_out, clear_field_STB, out_26);
  or or_1 (or_1_out, cursor_1_is_enter, change_cell_state);
  Multiplexer #(.disabled(0), .enable("false")) multiplexer_1 (
    .in0(or_1_out), .in1(change_cell_state), .out(multiplexer_1_out), .sel(game_ON));
  assign controlled_buffer_2_out = decoder_1_out0 ? I_Odata : 8'bz;  // Controlled_Buffer controlled_buffer_2
  or or_2 (or_2_out, decoder_1_out0, drow);
  not not_3 (not_3_out, or_2_out);
  Decoder #(.disabled(0)) decoder_2 (.out1(decoder_2_out1), .sel(In_out), .en(and_5_out));  // open: out0
  Decoder #(.disabled(0)) decoder_3 (.out0(change_cell_state), .sel(In_out), .en(and_6_out));  // open: out1
  Decoder #(.disabled(0)) decoder_4 (.out1(decoder_4_out1), .sel(In_out), .en(and_7_out));  // open: out0
  assign I_Odata = decoder_4_out1 ? count_of_neighbors : 8'bz;  // Controlled_Buffer controlled_buffer_3
  Decoder #(.disabled(0)) decoder_5 (.out1(decoder_5_out1), .sel(In_out), .en(and_8_out));  // open: out0
  assign I_Odata = decoder_5_out1 ? register_3_q : 8'bz;  // Controlled_Buffer controlled_buffer_4
  Decoder #(.disabled(0)) decoder_6 (.out0(code), .out1(data), .sel(cdm_8e_1_p5), .en(mem));
  assign I_Odata = not_4_out ? cdm_8e_1_p9 : 8'bz;  // Controlled_Buffer controlled_buffer_5
  not not_4 (not_4_out, In_out);
  Multiplexer #(.width(5), .enable("false")) multiplexer_2 (.in0(X), .in1(r_X), .out(multiplexer_2_out), .sel(drow));
  Multiplexer #(.width(5), .enable("false")) multiplexer_3 (.in0(Y), .in1(r_Y), .out(multiplexer_3_out), .sel(drow));
  or or_3 (or_3_out, clear_field_t, and_3_out);
  assign I_Odata = decoder_1_out1 ? {register_1_q, Y} : 8'bz;  // Controlled_Buffer controlled_buffer_6
  Register register_1 (.D(controlled_buffer_2_out), .Q({register_1_q, Y}), .clk(not_5_out));  // open: en, clr
  Pull_Resistor pull_resistor_1 (.node(pull_resistor_10_node[7]));
  Pull_Resistor pull_resistor_2 (.node(pull_resistor_10_node[6]));
  not not_5 (not_5_out, not_3_out);
  assign controlled_buffer_2_out = drow ? {pull_resistor_10_node, curs_Y} : 8'bz;  // Controlled_Buffer controlled_buffer_7
  assign I_Odata = decoder_2_out1 ? register_2_q : 8'bz;  // Controlled_Buffer controlled_buffer_8
  Register register_2 (.D(birth), .Q(register_2_q), .clk(xnor_1_out));  // open: en, clr
  xnor xnor_1 (xnor_1_out, game_ON, not_7_out);
  Register register_3 (
    .D({pull_resistor_3_node, death_cond__if_null}), .Q(register_3_q), .clk(xnor_2_out));  // open: en, clr
  Pull_Resistor pull_resistor_3 (.node(pull_resistor_3_node[1]));
  Pull_Resistor pull_resistor_4 (.node(pull_resistor_3_node[2]));
  Pull_Resistor pull_resistor_5 (.node(pull_resistor_3_node[3]));
  Pull_Resistor pull_resistor_6 (.node(pull_resistor_3_node[4]));
  Pull_Resistor pull_resistor_7 (.node(pull_resistor_3_node[5]));
  xnor xnor_2 (xnor_2_out, game_ON, not_8_out);
  Pull_Resistor pull_resistor_8 (.node(pull_resistor_3_node[6]));
  Pull_Resistor pull_resistor_9 (.node(pull_resistor_3_node[7]));
  // Probe on I_Oadr
  or or_4 (or_4_out, drow, game_ON);
  not not_6 (not_6_out, or_4_out);
  Multiplexer #(.width(5), .disabled(0), .enable("false")) multiplexer_4 (
    .in0(multiplexer_2_out), .in1(curs_X), .out(multiplexer_4_out), .sel(not_6_out));
  Multiplexer #(.width(5), .disabled(0), .enable("false")) multiplexer_5 (
    .in0(curs_Y), .in1(multiplexer_3_out), .out(multiplexer_5_out), .sel(or_5_out));
  or or_5 (or_5_out, drow, game_ON);
  write_buffer write_buffer_1 (
    .clear(or_3_out), .write_not(multiplexer_1_out), .row(multiplexer_5_out), .row0(write_buffer_1_row0),
    .row1(write_buffer_1_row1), .row2(write_buffer_1_row2), .row3(write_buffer_1_row3),
    .row4(write_buffer_1_row4), .row5(write_buffer_1_row5), .row6(write_buffer_1_row6),
    .row7(write_buffer_1_row7), .row8(write_buffer_1_row8), .row9(write_buffer_1_row9),
    .row10(write_buffer_1_row10), .row11(write_buffer_1_row11), .row12(write_buffer_1_row12),
    .row13(write_buffer_1_row13), .row14(write_buffer_1_row14), .row15(write_buffer_1_row15),
    .row0_2(write_buffer_1_row0_2), .row0_3(write_buffer_1_row0_3), .row0_4(write_buffer_1_row0_4),
    .row0_5(write_buffer_1_row0_5), .row0_6(write_buffer_1_row0_6), .row0_7(write_buffer_1_row0_7),
    .row0_8(write_buffer_1_row0_8), .row0_9(write_buffer_1_row0_9), .row0_10(write_buffer_1_row0_10),
    .row0_11(write_buffer_1_row0_11), .row0_12(write_buffer_1_row0_12), .row0_13(write_buffer_1_row0_13),
    .row0_14(write_buffer_1_row0_14), .row0_15(write_buffer_1_row0_15), .row0_16(write_buffer_1_row0_16),
    .row0_17(write_buffer_1_row0_17), .\input (converter_1_converted_row), .shrink(counter_1_q));
  Comparator #(.width(16)) comparator_1 (.a(I_Oadr), .b({16{1'b0}}), .eq(comparator_1_eq));  // open: gt, lt
  and and_4 (and_4_out, comparator_1_eq, I_Osel);
  Pull_Resistor pull_resistor_10 (.node(pull_resistor_10_node[5]));
  Comparator #(.width(16)) comparator_2 (.a(I_Oadr), .b(16'h3), .eq(comparator_2_eq));  // open: gt, lt
  and and_5 (and_5_out, comparator_2_eq, I_Osel);
  not not_7 (not_7_out, game_ON);
  Comparator #(.width(16)) comparator_3 (.a(I_Oadr), .b(16'h6), .eq(comparator_3_eq));  // open: gt, lt
  and and_6 (and_6_out, comparator_3_eq, I_Osel);
  Comparator #(.width(16)) comparator_4 (.a(I_Oadr), .b(16'h9), .eq(comparator_4_eq));  // open: gt, lt
  and and_7 (and_7_out, comparator_4_eq, I_Osel);
  Comparator #(.width(16)) comparator_5 (.a(I_Oadr), .b(16'he), .eq(comparator_5_eq));  // open: gt, lt
  and and_8 (and_8_out, comparator_5_eq, I_Osel);
  not not_8 (not_8_out, game_ON);
  and and_9 (and_9_out, or_7_out, or_6_out);
  or or_6 (or_6_out, comparator_6_gt, comparator_6_eq);
  Comparator #(.width(16)) comparator_6 (
    .a(I_Oadr), .b({16{1'b0}}), .gt(comparator_6_gt), .eq(comparator_6_eq));  // open: lt
  or or_7 (or_7_out, comparator_7_eq, comparator_7_lt);
  Comparator #(.width(16)) comparator_7 (
    .a(I_Oadr), .b(16'h1f), .eq(comparator_7_eq), .lt(comparator_7_lt));  // open: gt
  Multiplexer #(.disabled(0), .enable("false")) multiplexer_6 (
    .in0(clock), .in1(wait_1_out_2), .out(multiplexer_6_out), .sel(game_ON));
  converter converter_1 (
    .row_0(write_buffer_1_row0), .row_1(write_buffer_1_row1), .row_2(write_buffer_1_row2),
    .row_3(write_buffer_1_row3), .row_4(write_buffer_1_row4), .row_5(write_buffer_1_row5),
    .row_6(write_buffer_1_row6), .row_7(write_buffer_1_row7), .row_8(write_buffer_1_row8),
    .row_9(write_buffer_1_row9), .row_10(write_buffer_1_row10), .row_11(write_buffer_1_row11),
    .row_12(write_buffer_1_row12), .row_13(write_buffer_1_row13), .row_14(write_buffer_1_row14),
    .row_15(write_buffer_1_row15), .row_16(write_buffer_1_row0_2), .row_17(write_buffer_1_row0_3),
    .row_18(write_buffer_1_row0_4), .row_19(write_buffer_1_row0_5), .row_20(write_buffer_1_row0_6),
    .row_21(write_buffer_1_row0_7), .row_22(write_buffer_1_row0_8), .row_23(write_buffer_1_row0_9),
    .row_24(write_buffer_1_row0_10), .row_25(write_buffer_1_row0_11), .row_26(write_buffer_1_row0_12),
    .row_27(write_buffer_1_row0_13), .row_28(write_buffer_1_row0_14), .row_29(write_buffer_1_row0_15),
    .row_30(write_buffer_1_row0_16), .row_31(write_buffer_1_row0_17),
    .converted_row(converter_1_converted_row), .Y(multiplexer_5_out), .X(multiplexer_4_out));
  ROM #(.addrWidth(16)) rom_1 (.addr(I_Oadr), .data(I_Odata), .sel(code));
  RAM #(.addrWidth(16)) ram_1 (.addr(I_Oadr), .data(I_Odata), .sel(RAM), .clk(clock), .ld(In_out));  // open: clr
  Counter #(.width(4), .max('hf)) counter_1 (
    .Q(counter_1_q), .clk(and_10_out), .clr(or_8_out));  // open: load, D, count, carry
  or or_8 (or_8_out, clear_field_STB, clear_field_t);
  and and_10 (and_10_out, creative__0____survival__1, update_fixed_buffer);
  \wait  wait_1 (.in_1(update_fixed_buffer), .out_2(wait_1_out_2));
  neghbors neghbors_1 (
    .row_0(fixed_buffer_1_row_0_2), .row_1(fixed_buffer_1_row_1_2), .row_2(fixed_buffer_1_row_2_2),
    .row_3(fixed_buffer_1_row_3_2), .row_4(fixed_buffer_1_row_4_2), .row_5(fixed_buffer_1_row_5_2),
    .row_6(fixed_buffer_1_row_6_2), .row_7(fixed_buffer_1_row_7_2), .row_8(fixed_buffer_1_row_8_2),
    .row_9(fixed_buffer_1_row_9_2), .row_10(fixed_buffer_1_row_10_2), .X(multiplexer_4_out),
    .row_11(fixed_buffer_1_row_11_2), .row_12(fixed_buffer_1_row_12_2), .row_13(fixed_buffer_1_row_13_2),
    .row_14(fixed_buffer_1_row_14_2), .row_15(fixed_buffer_1_row_15_2), .row_16(fixed_buffer_1_row_16_2),
    .row_17(fixed_buffer_1_row_17_2), .row_18(fixed_buffer_1_row_18_2), .row_19(fixed_buffer_1_row_19_2),
    .row_20(fixed_buffer_1_row_20_2), .row_21(fixed_buffer_1_row_21_2), .row_22(fixed_buffer_1_row_22_2),
    .row_23(fixed_buffer_1_row_23_2), .row_24(fixed_buffer_1_row_24_2), .row_25(fixed_buffer_1_row_25_2),
    .row_26(fixed_buffer_1_row_26_2), .row_27(fixed_buffer_1_row_27_2), .row_28(fixed_buffer_1_row_28_2),
    .row_29(fixed_buffer_1_row_29_2), .row_30(fixed_buffer_1_row_30_2), .row_31(fixed_buffer_1_row_31_2),
    .row_is_null(is_row_null), .bit_state(cell_state), .count_of_neghbors(count_of_neighbors),
    .Y(multiplexer_5_out));
  fixed_buffer fixed_buffer_1 (
    .update(multiplexer_6_out), .row_0(write_buffer_1_row0), .row_1(write_buffer_1_row1),
    .row_2(write_buffer_1_row2), .row_3(write_buffer_1_row3), .row_4(write_buffer_1_row4),
    .row_5(write_buffer_1_row5), .row_6(write_buffer_1_row6), .row_7(write_buffer_1_row7),
    .row_8(write_buffer_1_row8), .row_9(write_buffer_1_row9), .row_10(write_buffer_1_row10),
    .row_11(write_buffer_1_row11), .row_12(write_buffer_1_row12), .row_13(write_buffer_1_row13),
    .row_14(write_buffer_1_row14), .row_15(write_buffer_1_row15), .row_16(write_buffer_1_row0_2),
    .row_17(write_buffer_1_row0_3), .row_18(write_buffer_1_row0_4), .row_19(write_buffer_1_row0_5),
    .row_20(write_buffer_1_row0_6), .row_21(write_buffer_1_row0_7), .row_22(write_buffer_1_row0_8),
    .row_23(write_buffer_1_row0_9), .row_24(write_buffer_1_row0_10), .row_25(write_buffer_1_row0_11),
    .row_26(write_buffer_1_row0_12), .row_27(write_buffer_1_row0_13), .row_28(write_buffer_1_row0_14),
    .row_29(write_buffer_1_row0_15), .row_30(write_buffer_1_row0_16), .row_31(write_buffer_1_row0_17),
    .row_0_2(fixed_buffer_1_row_0_2), .row_1_2(fixed_buffer_1_row_1_2), .row_2_2(fixed_buffer_1_row_2_2),
    .row_3_2(fixed_buffer_1_row_3_2), .row_4_2(fixed_buffer_1_row_4_2), .row_5_2(fixed_buffer_1_row_5_2),
    .row_6_2(fixed_buffer_1_row_6_2), .row_7_2(fixed_buffer_1_row_7_2), .row_8_2(fixed_buffer_1_row_8_2),
    .row_9_2(fixed_buffer_1_row_9_2), .row_10_2(fixed_buffer_1_row_10_2), .row_11_2(fixed_buffer_1_row_11_2),
    .row_12_2(fixed_buffer_1_row_12_2), .row_13_2(fixed_buffer_1_row_13_2),
    .row_14_2(fixed_buffer_1_row_14_2), .row_15_2(fixed_buffer_1_row_15_2),
    .row_16_2(fixed_buffer_1_row_16_2), .row_17_2(fixed_buffer_1_row_17_2),
    .row_18_2(fixed_buffer_1_row_18_2), .row_19_2(fixed_buffer_1_row_19_2),
    .row_20_2(fixed_buffer_1_row_20_2), .row_21_2(fixed_buffer_1_row_21_2),
    .row_22_2(fixed_buffer_1_row_22_2), .row_23_2(fixed_buffer_1_row_23_2),
    .row_24_2(fixed_buffer_1_row_24_2), .row_25_2(fixed_buffer_1_row_25_2),
    .row_26_2(fixed_buffer_1_row_26_2), .row_27_2(fixed_buffer_1_row_27_2),
    .row_28_2(fixed_buffer_1_row_28_2), .row_29_2(fixed_buffer_1_row_29_2),
    .row_30_2(fixed_buffer_1_row_30_2), .row_31_2(fixed_buffer_1_row_31_2));
  Decoder #(.disabled(0)) decoder_7 (.out0(decoder_7_out0), .out1(decoder_7_out1), .sel(In_out), .en(and_11_out));
  Decoder #(.disabled(0)) decoder_8 (.out1(decoder_8_out1), .sel(In_out), .en(and_13_out));  // open: out0
  assign I_Odata = decoder_8_out1 ? {pull_resistor_11_node, is_row_null} : 8'bz;  // Controlled_Buffer controlled_buffer_9
  // Probe on I_Odata
  // Debugger debugger_1: pin names not known
  assign I_Odata = decoder_7_out1 ? {register_4_q, X} : 8'bz;  // Controlled_Buffer controlled_buffer_10
  assign controlled_buffer_11_out = decoder_7_out0 ? I_Odata : 8'bz;  // Controlled_Buffer controlled_buffer_11
  not not_9 (not_9_out, not_10_out);
  or or_9 (or_9_out, decoder_7_out0, drow);
  not not_10 (not_10_out, or_9_out);
  assign controlled_buffer_11_out = drow ? {pull_resistor_18_node, curs_X} : 8'bz;  // Controlled_Buffer controlled_buffer_12
  Decoder #(.disabled(0)) decoder_9 (.out1(decoder_9_out1), .sel(In_out), .en(and_14_out));  // open: out0
  Decoder #(.disabled(0)) decoder_10 (.out0(update_fixed_buffer), .sel(In_out), .en(and_12_out));  // open: out1
  Comparator #(.width(16)) comparator_8 (.a(I_Oadr), .b(16'ha), .eq(comparator_8_eq));  // open: gt, lt
  Pull_Resistor pull_resistor_11 (.node(pull_resistor_11_node[1]));
  Pull_Resistor pull_resistor_12 (.node(pull_resistor_11_node[2]));
  Pull_Resistor pull_resistor_13 (.node(pull_resistor_11_node[3]));
  Pull_Resistor pull_resistor_14 (.node(pull_resistor_11_node[4]));
  Pull_Resistor pull_resistor_15 (.node(pull_resistor_11_node[5]));
  Pull_Resistor pull_resistor_16 (.node(pull_resistor_11_node[6]));
  Pull_Resistor pull_resistor_17 (.node(pull_resistor_11_node[7]));
  Decoder #(.disabled(0)) decoder_11 (.out0(decoder_11_out0), .out1(decoder_11_out1), .sel(In_out), .en(and_15_out));
  survival survival_1 (
    .WIN_1__or_LOSE_0(WIN___LOSE), .row_0(fixed_buffer_1_row_0_2), .row_1(fixed_buffer_1_row_1_2),
    .row_2(fixed_buffer_1_row_2_2), .row_3(fixed_buffer_1_row_3_2), .row_4(fixed_buffer_1_row_4_2),
    .row_5(fixed_buffer_1_row_5_2), .row_6(fixed_buffer_1_row_6_2), .row_7(fixed_buffer_1_row_7_2),
    .row_8(fixed_buffer_1_row_8_2), .row_9(fixed_buffer_1_row_9_2), .row_10(fixed_buffer_1_row_10_2),
    .row_11(fixed_buffer_1_row_11_2), .row_12(fixed_buffer_1_row_12_2), .row_13(fixed_buffer_1_row_13_2),
    .row_14(fixed_buffer_1_row_14_2), .row_15(fixed_buffer_1_row_15_2), .row_16(fixed_buffer_1_row_16_2),
    .row_17(fixed_buffer_1_row_17_2), .row_18(fixed_buffer_1_row_18_2), .row_19(fixed_buffer_1_row_19_2),
    .row_20(fixed_buffer_1_row_20_2), .row_21(fixed_buffer_1_row_21_2), .row_22(fixed_buffer_1_row_22_2),
    .row_23(fixed_buffer_1_row_23_2), .row_24(fixed_buffer_1_row_24_2), .row_25(fixed_buffer_1_row_25_2),
    .row_26(fixed_buffer_1_row_26_2), .row_27(fixed_buffer_1_row_27_2), .row_28(fixed_buffer_1_row_28_2),
    .row_29(fixed_buffer_1_row_29_2), .row_30(fixed_buffer_1_row_30_2), .row_31(fixed_buffer_1_row_31_2),
    .no_any_alive(no_any_alive));
  Comparator #(.width(16)) comparator_9 (.a(I_Oadr), .b(16'h1), .eq(comparator_9_eq));  // open: gt, lt
  and and_11 (and_11_out, comparator_9_eq, I_Osel);
  Register register_4 (.D(controlled_buffer_11_out), .Q({register_4_q, X}), .clk(not_9_out));  // open: en, clr
  Pull_Resistor pull_resistor_18 (.node(pull_resistor_18_node[5]));
  Pull_Resistor pull_resistor_19 (.node(pull_resistor_18_node[7]));
  Pull_Resistor pull_resistor_20 (.node(pull_resistor_18_node[6]));
  Comparator #(.width(16)) comparator_10 (.a(I_Oadr), .b(16'h4), .eq(comparator_10_eq));  // open: gt, lt
  assign I_Odata = decoder_9_out1 ? register_5_q : 8'bz;  // Controlled_Buffer controlled_buffer_13
  Register register_5 (.D(survival), .Q(register_5_q), .clk(xnor_3_out));  // open: en, clr
  xnor xnor_3 (xnor_3_out, game_ON, not_11_out);
  not not_11 (not_11_out, game_ON);
  Comparator #(.width(16)) comparator_11 (.a(I_Oadr), .b(16'h7), .eq(comparator_11_eq));  // open: gt, lt
  and and_12 (and_12_out, comparator_11_eq, I_Osel);
  and and_13 (and_13_out, comparator_8_eq, I_Osel);
  assign I_Odata = decoder_11_out1 ? {register_6_q, drow} : 8'bz;  // Controlled_Buffer controlled_buffer_14
  not not_12 (not_12_out[0], drow);
  Keyboard keyboard_1 (.clk(clock), .data(cursor_t));  // open: re, clr, avail
  zone_visualization zone_visualization_1 (
    .Number_of_dead_zones(counter_1_q), .row_0(fixed_buffer_1_row_0_2), .row_1(fixed_buffer_1_row_1_2),
    .row_2(fixed_buffer_1_row_2_2), .row_3(fixed_buffer_1_row_3_2), .row_4(fixed_buffer_1_row_4_2),
    .row_5(fixed_buffer_1_row_5_2), .row_6(fixed_buffer_1_row_6_2), .row_7(fixed_buffer_1_row_7_2),
    .row_8(fixed_buffer_1_row_8_2), .row_9(fixed_buffer_1_row_9_2), .row_10(fixed_buffer_1_row_10_2),
    .row_11(fixed_buffer_1_row_11_2), .row_12(fixed_buffer_1_row_12_2), .row_13(fixed_buffer_1_row_13_2),
    .row_14(fixed_buffer_1_row_14_2), .row_15(fixed_buffer_1_row_15_2), .row_16(fixed_buffer_1_row_16_2),
    .row_17(fixed_buffer_1_row_17_2), .row_18(fixed_buffer_1_row_18_2), .row_19(fixed_buffer_1_row_19_2),
    .row_20(fixed_buffer_1_row_20_2), .row_21(fixed_buffer_1_row_21_2), .row_22(fixed_buffer_1_row_22_2),
    .row_23(fixed_buffer_1_row_23_2), .row_24(fixed_buffer_1_row_24_2), .row_25(fixed_buffer_1_row_25_2),
    .row_26(fixed_buffer_1_row_26_2), .row_27(fixed_buffer_1_row_27_2), .row_28(fixed_buffer_1_row_28_2),
    .row_29(fixed_buffer_1_row_29_2), .row_30(fixed_buffer_1_row_30_2), .row_31(fixed_buffer_1_row_31_2),
    .row_0_2(zone_visualization_1_row_0_2), .row_1_2(zone_visualization_1_row_1_2),
    .row_2_2(zone_visualization_1_row_2_2), .row_3_2(zone_visualization_1_row_3_2),
    .row_4_2(zone_visualization_1_row_4_2), .row_5_2(zone_visualization_1_row_5_2),
    .row_6_2(zone_visualization_1_row_6_2), .row_7_2(zone_visualization_1_row_7_2),
    .row_8_2(zone_visualization_1_row_8_2), .row_9_2(zone_visualization_1_row_9_2),
    .row_10_2(zone_visualization_1_row_10_2), .row_11_2(zone_visualization_1_row_11_2),
    .row_12_2(zone_visualization_1_row_12_2), .row_13_2(zone_visualization_1_row_13_2),
    .row_14_2(zone_visualization_1_row_14_2), .row_15_2(zone_visualization_1_row_15_2),
    .row_16_2(zone_visualization_1_row_16_2), .row_17_2(zone_visualization_1_row_17_2),
    .row_18_2(zone_visualization_1_row_18_2), .row_19_2(zone_visualization_1_row_19_2),
    .row_20_2(zone_visualization_1_row_20_2), .row_21_2(zone_visualization_1_row_21_2),
    .row_22_2(zone_visualization_1_row_22_2), .row_23_2(zone_visualization_1_row_23_2),
    .row_24_2(zone_visualization_1_row_24_2), .row_25_2(zone_visualization_1_row_25_2),
    .row_26_2(zone_visualization_1_row_26_2), .row_27_2(zone_visualization_1_row_27_2),
    .row_28_2(zone_visualization_1_row_28_2), .row_29_2(zone_visualization_1_row_29_2),
    .row_30_2(zone_visualization_1_row_30_2), .row_31_2(zone_visualization_1_row_31_2));
  and and_14 (and_14_out, comparator_10_eq, I_Osel);
  Comparator #(.width(16)) comparator_12 (.a(I_Oadr), .b(16'hf), .eq(comparator_12_eq));  // open: gt, lt
  and and_15 (and_15_out, comparator_12_eq, I_Osel);
  Register register_6 (.D({register_6_q, not_12_out[0]}), .Q({register_6_q, drow}), .clk(or_10_out));  // open: en, clr
  or or_10 (or_10_out, drow_pattern, decoder_11_out0);
  Multiplexer #(.enable("false")) multiplexer_7 (.in0(clock), .in1(out_26), .out(multiplexer_7_out), .sel(out_26));
  cursor_visualization cursor_visualization_1 (
    .row_0(zone_visualization_1_row_0_2), .row_1(zone_visualization_1_row_1_2),
    .row_2(zone_visualization_1_row_2_2), .row_3(zone_visualization_1_row_3_2),
    .row_4(zone_visualization_1_row_4_2), .row_5(zone_visualization_1_row_5_2),
    .row_6(zone_visualization_1_row_6_2), .row_7(zone_visualization_1_row_7_2),
    .row_8(zone_visualization_1_row_8_2), .row_9(zone_visualization_1_row_9_2),
    .row_10(zone_visualization_1_row_10_2), .row_11(zone_visualization_1_row_11_2),
    .row_12(zone_visualization_1_row_12_2), .row_13(zone_visualization_1_row_13_2),
    .row_14(zone_visualization_1_row_14_2), .row_15(zone_visualization_1_row_15_2),
    .row_16(zone_visualization_1_row_16_2), .row_17(zone_visualization_1_row_17_2),
    .row_18(zone_visualization_1_row_18_2), .row_19(zone_visualization_1_row_19_2),
    .row_20(zone_visualization_1_row_20_2), .row_21(zone_visualization_1_row_21_2),
    .row_22(zone_visualization_1_row_22_2), .row_23(zone_visualization_1_row_23_2),
    .row_24(zone_visualization_1_row_24_2), .row_25(zone_visualization_1_row_25_2),
    .row_26(zone_visualization_1_row_26_2), .row_27(zone_visualization_1_row_27_2),
    .row_28(zone_visualization_1_row_28_2), .row_29(zone_visualization_1_row_29_2),
    .row_30(zone_visualization_1_row_30_2), .row_31(zone_visualization_1_row_31_2),
    .row_0_2(cursor_visualization_1_row_0_2), .row_1_2(cursor_visualization_1_row_1_2),
    .row_2_2(cursor_visualization_1_row_2_2), .row_3_2(cursor_visualization_1_row_3_2),
    .row_4_2(cursor_visualization_1_row_4_2), .row_5_2(cursor_visualization_1_row_5_2),
    .row_6_2(cursor_visualization_1_row_6_2), .row_7_2(cursor_visualization_1_row_7_2),
    .row_8_2(cursor_visualization_1_row_8_2), .row_9_2(cursor_visualization_1_row_9_2),
    .row_10_2(cursor_visualization_1_row_10_2), .row_11_2(cursor_visualization_1_row_11_2),
    .row_12_2(cursor_visualization_1_row_12_2), .row_13_2(cursor_visualization_1_row_13_2),
    .row_14_2(cursor_visualization_1_row_14_2), .row_15_2(cursor_visualization_1_row_15_2),
    .row_16_2(cursor_visualization_1_row_16_2), .row_17_2(cursor_visualization_1_row_17_2),
    .row_18_2(cursor_visualization_1_row_18_2), .row_19_2(cursor_visualization_1_row_19_2),
    .row_20_2(cursor_visualization_1_row_20_2), .row_21_2(cursor_visualization_1_row_21_2),
    .row_22_2(cursor_visualization_1_row_22_2), .row_23_2(cursor_visualization_1_row_23_2),
    .row_24_2(cursor_visualization_1_row_24_2), .row_25_2(cursor_visualization_1_row_25_2),
    .row_26_2(cursor_visualization_1_row_26_2), .row_27_2(cursor_visualization_1_row_27_2),
    .row_28_2(cursor_visualization_1_row_28_2), .row_29_2(cursor_visualization_1_row_29_2),
    .row_30_2(cursor_visualization_1_row_30_2), .row_31_2(cursor_visualization_1_row_31_2),
    .Y(multiplexer_5_out), .X(multiplexer_4_out), .on_off(multiplexer_7_out));
  Decoder #(.disabled(0)) decoder_12 (.out0(show_result), .sel(In_out), .en(and_16_out));  // open: out1
  DotMatrix #(.inputtype("row"), .matrixcols(32), .matrixrows(32)) dotmatrix_1 (
    .row0(cursor_visualization_1_row_0_2), .row1(cursor_visualization_1_row_1_2),
    .row2(cursor_visualization_1_row_2_2), .row3(cursor_visualization_1_row_3_2),
    .row4(cursor_visualization_1_row_4_2), .row5(cursor_visualization_1_row_5_2),
    .row6(cursor_visualization_1_row_6_2), .row7(cursor_visualization_1_row_7_2),
    .row8(cursor_visualization_1_row_8_2), .row9(cursor_visualization_1_row_9_2),
    .row10(cursor_visualization_1_row_10_2), .row11(cursor_visualization_1_row_11_2),
    .row12(cursor_visualization_1_row_12_2), .row13(cursor_visualization_1_row_13_2),
    .row14(cursor_visualization_1_row_14_2), .row15(cursor_visualization_1_row_15_2),
    .row16(cursor_visualization_1_row_16_2), .row17(cursor_visualization_1_row_17_2),
    .row18(cursor_visualization_1_row_18_2), .row19(cursor_visualization_1_row_19_2),
    .row20(cursor_visualization_1_row_20_2), .row21(cursor_visualization_1_row_21_2),
    .row22(cursor_visualization_1_row_22_2), .row23(cursor_visualization_1_row_23_2),
    .row24(cursor_visualization_1_row_24_2), .row25(cursor_visualization_1_row_25_2),
    .row26(cursor_visualization_1_row_26_2), .row27(cursor_visualization_1_row_27_2),
    .row28(cursor_visualization_1_row_28_2), .row29(cursor_visualization_1_row_29_2),
    .row30(cursor_visualization_1_row_30_2), .row31(cursor_visualization_1_row_31_2));
  Decoder #(.disabled(0)) decoder_13 (.out0(decoder_13_out0), .out1(decoder_13_out1), .sel(In_out), .en(and_18_out));
  not not_13 (not_13_out[0], game_ON);
  Decoder #(.disabled(0)) decoder_14 (.out1(decoder_14_out1), .sel(In_out), .en(and_19_out));  // open: out0
  Decoder #(.disabled(0)) decoder_15 (.out1(decoder_15_out1), .sel(In_out), .en(and_20_out));  // open: out0
  assign I_Odata = decoder_15_out1 ? {pull_resistor_28_node, cell_state} : 8'bz;  // Controlled_Buffer controlled_buffer_15
  Comparator #(.width(16)) comparator_13 (.a(I_Oadr), .b(16'hb), .eq(comparator_13_eq));  // open: gt, lt
  not not_14 (death_cond__if_null, survival_cond__if_null);
  Button u_drow_pattern (.out(drow_pattern));
  status_bar status_bar_1 (
    .game_ON___OFF(game_ON), .creative___survival(creative__0____survival__1), .WIN___LOSE(WIN___LOSE),
    .cursor({curs_Y, curs_X}), .show_result(show_result), .out_6(stb_0), .out_7(stb_1), .out_8(stb_2),
    .out_10(stb_3), .out_11(stb_4), .out_12(stb_5), .out_13(stb_6), .clear_field(clear_field_STB));
  assign I_Odata = decoder_13_out1 ? {not_13_out[7:1], game_ON} : 8'bz;  // Controlled_Buffer controlled_buffer_16
  Register register_7 (
    .D(not_13_out), .Q({not_13_out[7:1], game_ON}), .clk(game_ON___OFF), .clr(decoder_13_out0));  // open: en
  assign I_Odata = decoder_14_out1 ? {pull_resistor_21_node, creative__0____survival__1} : 8'bz;  // Controlled_Buffer controlled_buffer_17
  Pull_Resistor pull_resistor_21 (.node(pull_resistor_21_node[1]));
  Pull_Resistor pull_resistor_22 (.node(pull_resistor_21_node[2]));
  Pull_Resistor pull_resistor_23 (.node(pull_resistor_21_node[3]));
  Pull_Resistor pull_resistor_24 (.node(pull_resistor_21_node[4]));
  Pull_Resistor pull_resistor_25 (.node(pull_resistor_21_node[5]));
  Pull_Resistor pull_resistor_26 (.node(pull_resistor_21_node[6]));
  Pull_Resistor pull_resistor_27 (.node(pull_resistor_21_node[7]));
  Pull_Resistor pull_resistor_28 (.node(pull_resistor_28_node[1]));
  Pull_Resistor pull_resistor_29 (.node(pull_resistor_28_node[2]));
  Pull_Resistor pull_resistor_30 (.node(pull_resistor_28_node[3]));
  Pull_Resistor pull_resistor_31 (.node(pull_resistor_28_node[4]));
  Pull_Resistor pull_resistor_32 (.node(pull_resistor_28_node[5]));
  Pull_Resistor pull_resistor_33 (.node(pull_resistor_28_node[6]));
  Pull_Resistor pull_resistor_34 (.node(pull_resistor_28_node[7]));
  and and_16 (and_16_out, comparator_13_eq, I_Osel);
  Decoder #(.disabled(0)) decoder_16 (.out1(decoder_16_out1), .sel(In_out), .en(and_21_out));  // open: out0
  and and_17 (clear_field_t, clear_field, out_26);
  Comparator #(.width(16)) comparator_14 (.a(I_Oadr), .b(16'h2), .eq(comparator_14_eq));  // open: gt, lt
  and and_18 (and_18_out, comparator_14_eq, I_Osel);
  not not_15 (out_26, game_ON);
  Comparator #(.width(16)) comparator_15 (.a(I_Oadr), .b(16'h5), .eq(comparator_15_eq));  // open: gt, lt
  and and_19 (and_19_out, comparator_15_eq, I_Osel);
  Comparator #(.width(16)) comparator_16 (.a(I_Oadr), .b(16'h8), .eq(comparator_16_eq));  // open: gt, lt
  and and_20 (and_20_out, comparator_16_eq, I_Osel);
  assign I_Odata = decoder_16_out1 ? register_8_q : 8'bz;  // Controlled_Buffer controlled_buffer_18
  Pull_Resistor pull_resistor_35 (.node(pull_resistor_35_node[3]));
  Pull_Resistor pull_resistor_36 (.node(pull_resistor_35_node[4]));
  Pull_Resistor pull_resistor_37 (.node(pull_resistor_35_node[5]));
  Pull_Resistor pull_resistor_38 (.node(pull_resistor_35_node[6]));
  Pull_Resistor pull_resistor_39 (.node(pull_resistor_35_node[7]));
  Decoder #(.disabled(0)) decoder_17 (.out1(decoder_17_out1), .sel(In_out), .en(and_22_out));  // open: out0
  assign I_Odata = decoder_17_out1 ? {pull_resistor_40_node, no_any_alive} : 8'bz;  // Controlled_Buffer controlled_buffer_19
  Comparator #(.width(16)) comparator_17 (.a(I_Oadr), .b(16'h10), .eq(comparator_17_eq));  // open: gt, lt
  and and_21 (and_21_out, comparator_17_eq, I_Osel);
  Register register_8 (
    .D({pull_resistor_35_node, ID_of_pattern}), .Q(register_8_q), .clk(drow_pattern));  // open: en, clr
  Comparator #(.width(16)) comparator_18 (.a(I_Oadr), .b(16'hc), .eq(comparator_18_eq));  // open: gt, lt
  Pull_Resistor pull_resistor_40 (.node(pull_resistor_40_node[1]));
  Pull_Resistor pull_resistor_41 (.node(pull_resistor_40_node[2]));
  Pull_Resistor pull_resistor_42 (.node(pull_resistor_40_node[3]));
  Pull_Resistor pull_resistor_43 (.node(pull_resistor_40_node[4]));
  Pull_Resistor pull_resistor_44 (.node(pull_resistor_40_node[5]));
  Pull_Resistor pull_resistor_45 (.node(pull_resistor_40_node[6]));
  Pull_Resistor pull_resistor_46 (.node(pull_resistor_40_node[7]));
  and and_22 (and_22_out, comparator_18_eq, I_Osel);
  Decoder #(.disabled(0)) decoder_18 (.out1(decoder_18_out1), .sel(In_out), .en(and_23_out));  // open: out0
  assign I_Odata = decoder_18_out1 ? register_9_q : 8'bz;  // Controlled_Buffer controlled_buffer_20
  Pull_Resistor pull_resistor_47 (.node(pull_resistor_47_node[4]));
  Pull_Resistor pull_resistor_48 (.node(pull_resistor_47_node[5]));
  Pull_Resistor pull_resistor_49 (.node(pull_resistor_47_node[6]));
  Pull_Resistor pull_resistor_50 (.node(pull_resistor_47_node[7]));
  Comparator #(.width(16)) comparator_19 (.a(I_Oadr), .b(16'hd), .eq(comparator_19_eq));  // open: gt, lt
  and and_23 (and_23_out, comparator_19_eq, I_Osel);
  Register register_9 (.D({pull_resistor_47_node, zone_width}), .Q(register_9_q), .clk(game_ON));  // open: en, clr

  // Other names for the same wires on the sheet: game_mode = creative__0____survival__1; bith_condition[7:0] = birth;
  //   game_OFF = out_26; game_ON_OFF = game_ON___OFF; rd_wr = In_out; row0[31:0] = row_0; row1[31:0] = row_1;
  //   row2[31:0] = row_2; row3[31:0] = row_3; row4[31:0] = row_4; row5[31:0] = row_5; row6[31:0] = row_6;
  //   row7[31:0] = row_7; row8[31:0] = row_8; row9[31:0] = row_9; row10[31:0] = row_10; row11[31:0] = row_11;
  //   row12[31:0] = row_12; row13[31:0] = row_13; row14[31:0] = row_14; row15[31:0] = row_15; row16[31:0] = row_16;
  //   row17[31:0] = row_17; row18[31:0] = row_18; row19[31:0] = row_19; row20[31:0] = row_20; row21[31:0] = row_21;
  //   row22[31:0] = row_22; row23[31:0] = row_23; row24[31:0] = row_24; row25[31:0] = row_25; row26[31:0] = row_26;
  //   row27[31:0] = row_27; row28[31:0] = row_28; row29[31:0] = row_29; row30[31:0] = row_30; row31[31:0] = row_31;
  //   survival_condition[7:0] = survival

  // Notes on the sheet:
  //   row (Y)
  //   bith condition
  //   change cell state
  //   count of neighbors
  //   death cond. if null
  //   contents of rom_1 (hex, n*v repeats v):
  //   256*0 ee 37 0 e1 5 5 e1 2 d7 5 e1 6 d2 e ba ee d 0 e1 5 d2 20 ee 3 d2 28 89 16 ba a e0 9 d0 6 a0 d0
  //   30 d1 1 a1 d7 d2 8 a e0 a d3 1 43 a7 98 8d 8a ee f5 d7 cd 80 d2 f bb f e0 7 d6 e 2 d2 f aa d2 f d0 2
  //   b1 5 e0 ef d1 3 b4 d1 20 d6 29 1 d1 4 b4 80 d1 28 d6 29 1 d0 5 b0 0 e0 f d0 31 d1 1 a1 d0 32 d1 1e
  //   a1 d2 0 ee b d0 31 d1 0 a1 d0 32 d1 1f a1 d0 5 b0 0 e0 17 d0 d b0 78 e1 3 ee 7 d0 c b0 0 e0 9 d0 b
  //   a0 d0 2 a0 ee a0 d0 30 d1 0 a1 d0 7 a0 d3 0 d0 31 b3 c3 d0 2 b0 0 e1 4 d6 38 1 d0 0 a3 d0 a b0 0 e1
  //   1b d3 1 d0 31 b3 d0 1 a3 d0 8 b0 d1 9 b5 c2 d6 2 1 c6 8f d0 32 b0 7c e9 ec c7 8f d0 32 b0 7c e9 cc
  //   d0 5 b0 0 e0 2 8e d0 5 b0 0 e1 14 d0 30 b0 0 e1 9 d0 2 a0 d6 38 1 ee 4 d6 7d 1 ee 14 d0 31 b1 8d a1
  //   d0 32 b1 d0 1f c2 32 d0 32 a2 c6 d6 7d 1 d0 0 b0 d1 1 b5 d2 10 ba a e1 5 d6 5e 2 d7 d3 1 7b e1 5 d6
  //   6c 2 d7 d3 2 7b e1 5 d6 75 2 d7 d3 3 7b e1 5 d6 8b 2 d7 d3 4 7b e1 5 d6 b5 2 d7 d3 5 7b e1 5 d6 e5 2
  //   d7 d3 6 7b e1 5 d6 27 3 d7 d3 7 7b e1 5 d6 55 3 d7 d7 d2 6 88 aa 8c 89 aa 8c aa 8d aa 8d aa d7 d2 6
  //   88 aa 8c aa 8c aa d7 d2 6 88 aa 8d aa 88 aa 8c 8c aa 8c 89 aa 89 aa 88 aa 8c 89 aa d7 d2 6 89 aa 89
  //   88 aa 8d 8d 88 aa 88 aa 8d 8c 8d aa 8c 8c 8d aa 89 aa 89 aa 89 aa 89 89 8c aa 8d 8d 8c aa 8c aa 8d
  //   88 8d aa d7 d2 6 88 aa 89 8c aa 89 aa 88 aa 88 aa 89 aa 4*8c aa 8d aa 88 aa 8d 8d aa 8d 88 aa 8d aa
  //   88 aa 88 aa 8d aa 4*8c aa 89 aa 88 aa d7 d2 6 aa 89 88 aa 88 aa 89 88 aa 89 aa 89 88 aa 88 aa 88 8d
  //   aa 8d aa 8d 8c aa 8c aa 8d aa 8d aa 8d aa 88 aa 88 8d aa 8d aa 8d 8c aa 8c aa 8c 89 aa 89 aa 89 8c
  //   aa 89 aa 89 aa 8d 8d 8c aa 8c 89 aa d7 d2 6 aa 89 aa 89 88 aa 89 89 aa 89 aa 88 aa 8d aa 8d 8d 8d aa
  //   88 8d aa 88 8d aa 88 88 88 aa 88 aa 8d aa 8c aa 8c 8c aa 8d 8c aa 8c aa d7 d2 6 aa 89 aa 8c 89 aa 89
  //   aa 88 88 8d aa 8d 88 aa 88 8d aa 8d 8c aa 8c 8d aa 8c 89 aa 8c 8d aa 8d aa d7 d4
  //   column (X)
  //   update fixed buffer
  //   is row null
  //   survival condition
  //   drow pattern
  //   show result
  //   game state
  //   game mode
  //   cell state
  //   ID of pattern
  //   no any alive
  //   zone width
endmodule

module write_buffer (
  input  clear,
  input  [31:0] \input ,
  input  [3:0] shrink,
  input  write_not,
  input  [4:0] row,
  output [31:0] row0,
  output [31:0] row1,
  output [31:0] row2,
  output [31:0] row3,
  output [31:0] row4,
  output [31:0] row5,
  output [31:0] row6,
  output [31:0] row7,
  output [31:0] row8,
  output [31:0] row9,
  output [31:0] row10,
  output [31:0] row11,
  output [31:0] row12,
  output [31:0] row13,
  output [31:0] row14,
  output [31:0] row15,
  output [31:0] row0_2,
  output [31:0] row0_3,
  output [31:0] row0_4,
  output [31:0] row0_5,
  output [31:0] row0_6,
  output [31:0] row0_7,
  output [31:0] row0_8,
  output [31:0] row0_9,
  output [31:0] row0_10,
  output [31:0] row0_11,
  output [31:0] row0_12,
  output [31:0] row0_13,
  output [31:0] row0_14,
  output [31:0] row0_15,
  output [31:0] row0_16,
  output [31:0] row0_17
);

  wire _1, _2, _3, _4, _5, _6, _7, _8, _9, _10, _11, _12, _13, _14, _15, block1, block2, block3, block4,
       block5, block6, block7, block8, block9, block10, block11, block12, block13, block14,
       multiplexer_2_out, multiplexer_3_out, multiplexer_4_out, multiplexer_5_out, multiplexer_6_out,
       multiplexer_7_out, multiplexer_8_out, multiplexer_9_out, multiplexer_10_out, multiplexer_11_out,
       multiplexer_12_out, multiplexer_13_out, multiplexer_14_out, multiplexer_15_out, multiplexer_16_out,
       multiplexer_17_out, multiplexer_18_out, multiplexer_19_out, multiplexer_20_out, multiplexer_21_out,
       multiplexer_22_out, multiplexer_23_out, multiplexer_24_out, multiplexer_25_out, multiplexer_26_out,
       multiplexer_27_out, multiplexer_28_out, multiplexer_29_out, multiplexer_30_out, multiplexer_31_out,
       not_1_out, not_2_out, not_3_out, not_4_out, not_5_out, not_6_out, not_7_out, not_8_out, not_9_out,
       not_10_out, not_11_out, not_12_out, not_13_out, not_14_out, not_15_out, not_16_out, not_17_out,
       not_18_out, not_19_out, not_20_out, not_21_out, not_22_out, not_23_out, not_24_out, not_25_out,
       not_26_out, not_27_out, not_28_out, not_29_out, not_30_out, not_31_out, not_32_out, not_33_out,
       not_34_out, not_35_out, not_36_out, not_37_out, not_38_out, not_39_out, not_40_out, not_41_out,
       not_42_out, not_43_out, not_44_out, not_45_out, not_46_out, not_47_out, not_48_out, not_49_out,
       not_50_out, not_51_out, not_52_out, not_53_out, not_54_out, not_55_out, not_56_out, not_57_out,
       not_58_out, not_59_out, not_60_out, row0_t, row1_t, row2_t, row3_t, row4_t, row5_t, row6_t, row7_t,
       row8_t, row9_t, row10_t, row11_t, row12_t, row13_t, row14_t, row15_t, row16, row17, row18, row19,
       row20, row21, row22, row23, row24, row25, row26, row27, row28, row29, row30, row31;
  wire [31:0] gaps, register_2_q, register_3_q, register_4_q, register_5_q, register_6_q, register_7_q,
       register_8_q, register_9_q, register_10_q, register_11_q, register_12_q, register_13_q, register_14_q,
       register_15_q, register_16_q, register_17_q, register_18_q, register_19_q, register_20_q,
       register_21_q, register_22_q, register_23_q, register_24_q, register_25_q, register_26_q,
       register_27_q, register_28_q, register_29_q, register_30_q, register_31_q, register_32_q;

  Decoder #(.select(4), .enable("false")) decoder_1 (
    .out1(_1), .out2(_2), .out3(_3), .out4(_4), .out5(_5), .out6(_6), .out7(_7), .out8(_8), .out9(_9),
    .out10(_10), .out11(_11), .out12(_12), .out13(_13), .out14(_14), .out15(_15), .sel(shrink));  // open: out0
  Multiplexer #(.select(4), .width(32), .disabled(0), .enable("false")) multiplexer_1 (
    .in0({32{1'b1}}), .in1(32'h7ffffffe), .in2(32'h3ffffffc), .in3(32'h1ffffff8), .in4(32'hffffff0),
    .in5(32'h7ffffe0), .in6(32'h3ffffc0), .in7(32'h1ffff80), .in8(32'hffff00), .in9(32'h7ffe00),
    .in10(32'h3ffc00), .in11(32'h1ff800), .in12(32'hff000), .in13(32'h7e000), .in14(32'h3c000),
    .in15(32'h18000), .out(gaps), .sel(shrink));
  or or_1 (block1, _1, _2, _3, _4, _5, _6, _7, _8, _9, _10, _11, _12, _13, _14, _15);
  or or_2 (block2, _2, _3, _4, _5, _6, _7, _8, _9, _10, _11, _12, _13, _14, _15);
  or or_3 (block3, _3, _4, _5, _6, _7, _8, _9, _10, _11, _12, _13, _14, _15);
  or or_4 (block4, _4, _5, _6, _7, _8, _9, _10, _11, _12, _13, _14, _15);
  or or_5 (block5, _5, _6, _7, _8, _9, _10, _11, _12, _13, _14, _15);
  or or_6 (block6, _6, _7, _8, _9, _10, _11, _12, _13, _14, _15);
  or or_7 (block7, _7, _8, _9, _10, _11, _12, _13, _14, _15);
  or or_8 (block8, _8, _9, _10, _11, _12, _13, _14, _15);
  or or_9 (block9, _9, _10, _11, _12, _13, _14, _15);
  or or_10 (block10, _10, _11, _12, _13, _14, _15);
  or or_11 (block11, _11, _12, _13, _14, _15);
  or or_12 (block12, _12, _13, _14, _15);
  or or_13 (block13, _13, _14, _15);
  or or_14 (block14, _14, _15);
  Decoder #(.select(5), .disabled(0)) decoder_2 (
    .out0(row0_t), .out1(row1_t), .out2(row2_t), .out3(row3_t), .out4(row4_t), .out5(row5_t), .out6(row6_t),
    .out7(row7_t), .out8(row8_t), .out9(row9_t), .out10(row10_t), .out11(row11_t), .out12(row12_t),
    .out13(row13_t), .out14(row14_t), .out15(row15_t), .out16(row16), .out17(row17), .out18(row18),
    .out19(row19), .out20(row20), .out21(row21), .out22(row22), .out23(row23), .out24(row24), .out25(row25),
    .out26(row26), .out27(row27), .out28(row28), .out29(row29), .out30(row30), .out31(row31), .sel(row),
    .en(write_not));
  not not_1 (not_1_out, block1);
  not not_2 (not_2_out, block2);
  not not_3 (not_3_out, block3);
  not not_4 (not_4_out, block4);
  not not_5 (not_5_out, block5);
  not not_6 (not_6_out, block6);
  not not_7 (not_7_out, block7);
  not not_8 (not_8_out, block8);
  not not_9 (not_9_out, block9);
  not not_10 (not_10_out, block10);
  not not_11 (not_11_out, block11);
  not not_12 (not_12_out, block12);
  not not_13 (not_13_out, block13);
  not not_14 (not_14_out, block14);
  not not_15 (not_15_out, _15);
  not not_16 (not_16_out, _15);
  not not_17 (not_17_out, block14);
  not not_18 (not_18_out, block13);
  not not_19 (not_19_out, block12);
  not not_20 (not_20_out, block11);
  not not_21 (not_21_out, block10);
  not not_22 (not_22_out, block9);
  not not_23 (not_23_out, block8);
  not not_24 (not_24_out, block7);
  not not_25 (not_25_out, block6);
  not not_26 (not_26_out, block5);
  not not_27 (not_27_out, block4);
  not not_28 (not_28_out, block3);
  not not_29 (not_29_out, block2);
  not not_30 (not_30_out, block1);
  Register #(.width(32)) register_1 (.D(\input ), .en(not_1_out), .Q(row0), .clk(row0_t), .clr(multiplexer_2_out));
  Register #(.width(32)) register_2 (
    .D(\input ), .en(not_2_out), .Q(register_2_q), .clk(row1_t), .clr(multiplexer_3_out));
  Register #(.width(32)) register_3 (
    .D(\input ), .en(not_3_out), .Q(register_3_q), .clk(row2_t), .clr(multiplexer_4_out));
  Register #(.width(32)) register_4 (
    .D(\input ), .en(not_4_out), .Q(register_4_q), .clk(row3_t), .clr(multiplexer_5_out));
  Register #(.width(32)) register_5 (
    .D(\input ), .en(not_5_out), .Q(register_5_q), .clk(row4_t), .clr(multiplexer_6_out));
  Register #(.width(32)) register_6 (
    .D(\input ), .en(not_6_out), .Q(register_6_q), .clk(row5_t), .clr(multiplexer_7_out));
  Register #(.width(32)) register_7 (
    .D(\input ), .en(not_7_out), .Q(register_7_q), .clk(row6_t), .clr(multiplexer_8_out));
  Register #(.width(32)) register_8 (
    .D(\input ), .en(not_8_out), .Q(register_8_q), .clk(row7_t), .clr(multiplexer_9_out));
  Register #(.width(32)) register_9 (
    .D(\input ), .en(not_9_out), .Q(register_9_q), .clk(row8_t), .clr(multiplexer_10_out));
  Register #(.width(32)) register_10 (
    .D(\input ), .en(not_10_out), .Q(register_10_q), .clk(row9_t), .clr(multiplexer_11_out));
  Register #(.width(32)) register_11 (
    .D(\input ), .en(not_11_out), .Q(register_11_q), .clk(row10_t), .clr(multiplexer_12_out));
  Register #(.width(32)) register_12 (
    .D(\input ), .en(not_12_out), .Q(register_12_q), .clk(row11_t), .clr(multiplexer_13_out));
  Register #(.width(32)) register_13 (
    .D(\input ), .en(not_13_out), .Q(register_13_q), .clk(row12_t), .clr(multiplexer_14_out));
  Register #(.width(32)) register_14 (
    .D(\input ), .en(not_14_out), .Q(register_14_q), .clk(row13_t), .clr(multiplexer_15_out));
  Register #(.width(32)) register_15 (
    .D(\input ), .en(not_15_out), .Q(register_15_q), .clk(row14_t), .clr(multiplexer_16_out));
  Register #(.width(32)) register_16 (.D(\input ), .Q(register_16_q), .clk(row15_t), .clr(clear));  // open: en
  Register #(.width(32)) register_17 (.D(\input ), .Q(register_17_q), .clk(row16), .clr(clear));  // open: en
  Register #(.width(32)) register_18 (
    .D(\input ), .en(not_16_out), .Q(register_18_q), .clk(row17), .clr(multiplexer_17_out));
  Register #(.width(32)) register_19 (
    .D(\input ), .en(not_17_out), .Q(register_19_q), .clk(row18), .clr(multiplexer_18_out));
  Register #(.width(32)) register_20 (
    .D(\input ), .en(not_18_out), .Q(register_20_q), .clk(row19), .clr(multiplexer_19_out));
  Register #(.width(32)) register_21 (
    .D(\input ), .en(not_19_out), .Q(register_21_q), .clk(row20), .clr(multiplexer_20_out));
  Register #(.width(32)) register_22 (
    .D(\input ), .en(not_20_out), .Q(register_22_q), .clk(row21), .clr(multiplexer_21_out));
  Register #(.width(32)) register_23 (
    .D(\input ), .en(not_21_out), .Q(register_23_q), .clk(row22), .clr(multiplexer_22_out));
  Register #(.width(32)) register_24 (
    .D(\input ), .en(not_22_out), .Q(register_24_q), .clk(row23), .clr(multiplexer_23_out));
  Register #(.width(32)) register_25 (
    .D(\input ), .en(not_23_out), .Q(register_25_q), .clk(row24), .clr(multiplexer_24_out));
  Register #(.width(32)) register_26 (
    .D(\input ), .en(not_24_out), .Q(register_26_q), .clk(row25), .clr(multiplexer_25_out));
  Register #(.width(32)) register_27 (
    .D(\input ), .en(not_25_out), .Q(register_27_q), .clk(row26), .clr(multiplexer_26_out));
  Register #(.width(32)) register_28 (
    .D(\input ), .en(not_26_out), .Q(register_28_q), .clk(row27), .clr(multiplexer_27_out));
  Register #(.width(32)) register_29 (
    .D(\input ), .en(not_27_out), .Q(register_29_q), .clk(row28), .clr(multiplexer_28_out));
  Register #(.width(32)) register_30 (
    .D(\input ), .en(not_28_out), .Q(register_30_q), .clk(row29), .clr(multiplexer_29_out));
  Register #(.width(32)) register_31 (
    .D(\input ), .en(not_29_out), .Q(register_31_q), .clk(row30), .clr(multiplexer_30_out));
  Register #(.width(32)) register_32 (
    .D(\input ), .en(not_30_out), .Q(register_32_q), .clk(row31), .clr(multiplexer_31_out));
  Multiplexer #(.disabled(0), .enable("false")) multiplexer_2 (
    .in0(clear), .in1(not_31_out), .out(multiplexer_2_out), .sel(block1));
  not not_31 (not_31_out, clear);
  Multiplexer #(.disabled(0), .enable("false")) multiplexer_3 (
    .in0(clear), .in1(not_32_out), .out(multiplexer_3_out), .sel(block2));
  not not_32 (not_32_out, clear);
  Multiplexer #(.disabled(0), .enable("false")) multiplexer_4 (
    .in0(clear), .in1(not_33_out), .out(multiplexer_4_out), .sel(block3));
  not not_33 (not_33_out, clear);
  Multiplexer #(.disabled(0), .enable("false")) multiplexer_5 (
    .in0(clear), .in1(not_34_out), .out(multiplexer_5_out), .sel(block4));
  not not_34 (not_34_out, clear);
  Multiplexer #(.disabled(0), .enable("false")) multiplexer_6 (
    .in0(clear), .in1(not_35_out), .out(multiplexer_6_out), .sel(block5));
  not not_35 (not_35_out, clear);
  Multiplexer #(.disabled(0), .enable("false")) multiplexer_7 (
    .in0(clear), .in1(not_36_out), .out(multiplexer_7_out), .sel(block6));
  not not_36 (not_36_out, clear);
  Multiplexer #(.disabled(0), .enable("false")) multiplexer_8 (
    .in0(clear), .in1(not_37_out), .out(multiplexer_8_out), .sel(block7));
  not not_37 (not_37_out, clear);
  Multiplexer #(.disabled(0), .enable("false")) multiplexer_9 (
    .in0(clear), .in1(not_38_out), .out(multiplexer_9_out), .sel(block8));
  not not_38 (not_38_out, clear);
  Multiplexer #(.disabled(0), .enable("false")) multiplexer_10 (
    .in0(clear), .in1(not_39_out), .out(multiplexer_10_out), .sel(block9));
  not not_39 (not_39_out, clear);
  Multiplexer #(.disabled(0), .enable("false")) multiplexer_11 (
    .in0(clear), .in1(not_40_out), .out(multiplexer_11_out), .sel(block10));
  not not_40 (not_40_out, clear);
  Multiplexer #(.disabled(0), .enable("false")) multiplexer_12 (
    .in0(clear), .in1(not_41_out), .out(multiplexer_12_out), .sel(block11));
  not not_41 (not_41_out, clear);
  Multiplexer #(.disabled(0), .enable("false")) multiplexer_13 (
    .in0(clear), .in1(not_42_out), .out(multiplexer_13_out), .sel(block12));
  not not_42 (not_42_out, clear);
  Multiplexer #(.disabled(0), .enable("false")) multiplexer_14 (
    .in0(clear), .in1(not_43_out), .out(multiplexer_14_out), .sel(block13));
  not not_43 (not_43_out, clear);
  Multiplexer #(.disabled(0), .enable("false")) multiplexer_15 (
    .in0(clear), .in1(not_44_out), .out(multiplexer_15_out), .sel(block14));
  not not_44 (not_44_out, clear);
  Multiplexer #(.disabled(0), .enable("false")) multiplexer_16 (
    .in0(clear), .in1(not_45_out), .out(multiplexer_16_out), .sel(_15));
  not not_45 (not_45_out, clear);
  Multiplexer #(.disabled(0), .enable("false")) multiplexer_17 (
    .in0(clear), .in1(not_46_out), .out(multiplexer_17_out), .sel(_15));
  not not_46 (not_46_out, clear);
  Multiplexer #(.disabled(0), .enable("false")) multiplexer_18 (
    .in0(clear), .in1(not_47_out), .out(multiplexer_18_out), .sel(block14));
  not not_47 (not_47_out, clear);
  Multiplexer #(.disabled(0), .enable("false")) multiplexer_19 (
    .in0(clear), .in1(not_48_out), .out(multiplexer_19_out), .sel(block13));
  not not_48 (not_48_out, clear);
  Multiplexer #(.disabled(0), .enable("false")) multiplexer_20 (
    .in0(clear), .in1(not_49_out), .out(multiplexer_20_out), .sel(block12));
  not not_49 (not_49_out, clear);
  Multiplexer #(.disabled(0), .enable("false")) multiplexer_21 (
    .in0(clear), .in1(not_50_out), .out(multiplexer_21_out), .sel(block11));
  not not_50 (not_50_out, clear);
  Multiplexer #(.disabled(0), .enable("false")) multiplexer_22 (
    .in0(clear), .in1(not_51_out), .out(multiplexer_22_out), .sel(block10));
  not not_51 (not_51_out, clear);
  Multiplexer #(.disabled(0), .enable("false")) multiplexer_23 (
    .in0(clear), .in1(not_52_out), .out(multiplexer_23_out), .sel(block9));
  not not_52 (not_52_out, clear);
  Multiplexer #(.disabled(0), .enable("false")) multiplexer_24 (
    .in0(clear), .in1(not_53_out), .out(multiplexer_24_out), .sel(block8));
  not not_53 (not_53_out, clear);
  Multiplexer #(.disabled(0), .enable("false")) multiplexer_25 (
    .in0(clear), .in1(not_54_out), .out(multiplexer_25_out), .sel(block7));
  not not_54 (not_54_out, clear);
  Multiplexer #(.disabled(0), .enable("false")) multiplexer_26 (
    .in0(clear), .in1(not_55_out), .out(multiplexer_26_out), .sel(block6));
  not not_55 (not_55_out, clear);
  Multiplexer #(.disabled(0), .enable("false")) multiplexer_27 (
    .in0(clear), .in1(not_56_out), .out(multiplexer_27_out), .sel(block5));
  not not_56 (not_56_out, clear);
  Multiplexer #(.disabled(0), .enable("false")) multiplexer_28 (
    .in0(clear), .in1(not_57_out), .out(multiplexer_28_out), .sel(block4));
  not not_57 (not_57_out, clear);
  Multiplexer #(.disabled(0), .enable("false")) multiplexer_29 (
    .in0(clear), .in1(not_58_out), .out(multiplexer_29_out), .sel(block3));
  not not_58 (not_58_out, clear);
  Multiplexer #(.disabled(0), .enable("false")) multiplexer_30 (
    .in0(clear), .in1(not_59_out), .out(multiplexer_30_out), .sel(block2));
  not not_59 (not_59_out, clear);
  Multiplexer #(.disabled(0), .enable("false")) multiplexer_31 (
    .in0(clear), .in1(not_60_out), .out(multiplexer_31_out), .sel(block1));
  not not_60 (not_60_out, clear);
  assign row1 = register_2_q & gaps;  // AND_Gate and_1, 32 bits wide
  assign row2 = register_3_q & gaps;  // AND_Gate and_2, 32 bits wide
  assign row3 = register_4_q & gaps;  // AND_Gate and_3, 32 bits wide
  assign row4 = register_5_q & gaps;  // AND_Gate and_4, 32 bits wide
  assign row5 = register_6_q & gaps;  // AND_Gate and_5, 32 bits wide
  assign row6 = register_7_q & gaps;  // AND_Gate and_6, 32 bits wide
  assign row7 = register_8_q & gaps;  // AND_Gate and_7, 32 bits wide
  assign row8 = register_9_q & gaps;  // AND_Gate and_8, 32 bits wide
  assign row9 = register_10_q & gaps;  // AND_Gate and_9, 32 bits wide
  assign row10 = register_11_q & gaps;  // AND_Gate and_10, 32 bits wide
  assign row11 = register_12_q & gaps;  // AND_Gate and_11, 32 bits wide
  assign row12 = register_13_q & gaps;  // AND_Gate and_12, 32 bits wide
  assign row13 = register_14_q & gaps;  // AND_Gate and_13, 32 bits wide
  assign row14 = register_15_q & gaps;  // AND_Gate and_14, 32 bits wide
  assign row15 = register_16_q & gaps;  // AND_Gate and_15, 32 bits wide
  assign row0_2 = register_17_q & gaps;  // AND_Gate and_16, 32 bits wide
  assign row0_3 = register_18_q & gaps;  // AND_Gate and_17, 32 bits wide
  assign row0_4 = register_19_q & gaps;  // AND_Gate and_18, 32 bits wide
  assign row0_5 = register_20_q & gaps;  // AND_Gate and_19, 32 bits wide
  assign row0_6 = register_21_q & gaps;  // AND_Gate and_20, 32 bits wide
  assign row0_7 = register_22_q & gaps;  // AND_Gate and_21, 32 bits wide
  assign row0_8 = register_23_q & gaps;  // AND_Gate and_22, 32 bits wide
  assign row0_9 = register_24_q & gaps;  // AND_Gate and_23, 32 bits wide
  assign row0_10 = register_25_q & gaps;  // AND_Gate and_24, 32 bits wide
  assign row0_11 = register_26_q & gaps;  // AND_Gate and_25, 32 bits wide
  assign row0_12 = register_27_q & gaps;  // AND_Gate and_26, 32 bits wide
  assign row0_13 = register_28_q & gaps;  // AND_Gate and_27, 32 bits wide
  assign row0_14 = register_29_q & gaps;  // AND_Gate and_28, 32 bits wide
  assign row0_15 = register_30_q & gaps;  // AND_Gate and_29, 32 bits wide
  assign row0_16 = register_31_q & gaps;  // AND_Gate and_30, 32 bits wide
  assign row0_17 = register_32_q & gaps;  // AND_Gate and_31, 32 bits wide

  // Other names for the same wires on the sheet: block15 = _15

  // Notes on the sheet:
  //   Masks
endmodule

module converter (
  input  [4:0] Y,
  input  [4:0] X,
  input  [31:0] row_0,
  input  [31:0] row_1,
  input  [31:0] row_2,
  input  [31:0] row_3,
  input  [31:0] row_4,
  input  [31:0] row_5,
  input  [31:0] row_6,
  input  [31:0] row_7,
  input  [31:0] row_8,
  input  [31:0] row_9,
  input  [31:0] row_10,
  input  [31:0] row_11,
  input  [31:0] row_12,
  input  [31:0] row_13,
  input  [31:0] row_14,
  input  [31:0] row_15,
  input  [31:0] row_16,
  input  [31:0] row_17,
  input  [31:0] row_18,
  input  [31:0] row_19,
  input  [31:0] row_20,
  input  [31:0] row_21,
  input  [31:0] row_22,
  input  [31:0] row_23,
  input  [31:0] row_24,
  input  [31:0] row_25,
  input  [31:0] row_26,
  input  [31:0] row_27,
  input  [31:0] row_28,
  input  [31:0] row_29,
  input  [31:0] row_30,
  input  [31:0] row_31,
  output [31:0] converted_row
);

  wire [31:0] and_1_out, and_2_out, multiplexer_1_out, not_1_out, not_2_out, shifter_1_out;

  Multiplexer #(.select(5), .width(32), .disabled(0), .enable("false")) multiplexer_1 (
    .in0(row_0), .in1(row_1), .in2(row_2), .in3(row_3), .in4(row_4), .in5(row_5), .in6(row_6), .in7(row_7),
    .in8(row_8), .in9(row_9), .in10(row_10), .in11(row_11), .in12(row_12), .in13(row_13), .in14(row_14),
    .in15(row_15), .in16(row_16), .in17(row_17), .in18(row_18), .in19(row_19), .in20(row_20), .in21(row_21),
    .in22(row_22), .in23(row_23), .in24(row_24), .in25(row_25), .in26(row_26), .in27(row_27), .in28(row_28),
    .in29(row_29), .in30(row_30), .in31(row_31), .out(multiplexer_1_out), .sel(Y));
  Shifter #(.width(32)) shifter_1 (.in(32'h1), .\dist (X), .out(shifter_1_out));
  assign not_1_out = ~shifter_1_out;  // NOT_Gate not_1, 32 bits wide
  assign not_2_out = ~multiplexer_1_out;  // NOT_Gate not_2, 32 bits wide
  assign and_1_out = not_1_out & multiplexer_1_out;  // AND_Gate and_1, 32 bits wide
  assign converted_row = and_1_out | and_2_out;  // OR_Gate or_1, 32 bits wide
  assign and_2_out = shifter_1_out & not_2_out;  // AND_Gate and_2, 32 bits wide

  // Other names for the same wires on the sheet: row0[31:0] = row_0; row1[31:0] = row_1; row2[31:0] = row_2;
  //   row3[31:0] = row_3; row4[31:0] = row_4; row5[31:0] = row_5; row6[31:0] = row_6; row7[31:0] = row_7;
  //   row8[31:0] = row_8; row9[31:0] = row_9; row10[31:0] = row_10; row11[31:0] = row_11; row12[31:0] = row_12;
  //   row13[31:0] = row_13; row14[31:0] = row_14; row15[31:0] = row_15; row16[31:0] = row_16; row17[31:0] = row_17;
  //   row18[31:0] = row_18; row19[31:0] = row_19; row20[31:0] = row_20; row21[31:0] = row_21; row22[31:0] = row_22;
  //   row23[31:0] = row_23; row24[31:0] = row_24; row25[31:0] = row_25; row26[31:0] = row_26; row27[31:0] = row_27;
  //   row28[31:0] = row_28; row29[31:0] = row_29; row30[31:0] = row_30; row31[31:0] = row_31
endmodule

module fixed_buffer (
  input  update,
  input  [31:0] row_0,
  input  [31:0] row_1,
  input  [31:0] row_2,
  input  [31:0] row_3,
  input  [31:0] row_4,
  input  [31:0] row_5,
  input  [31:0] row_6,
  input  [31:0] row_7,
  input  [31:0] row_8,
  input  [31:0] row_9,
  input  [31:0] row_10,
  input  [31:0] row_11,
  input  [31:0] row_12,
  input  [31:0] row_13,
  input  [31:0] row_14,
  input  [31:0] row_15,
  input  [31:0] row_16,
  input  [31:0] row_17,
  input  [31:0] row_18,
  input  [31:0] row_19,
  input  [31:0] row_20,
  input  [31:0] row_21,
  input  [31:0] row_22,
  input  [31:0] row_23,
  input  [31:0] row_24,
  input  [31:0] row_25,
  input  [31:0] row_26,
  input  [31:0] row_27,
  input  [31:0] row_28,
  input  [31:0] row_29,
  input  [31:0] row_30,
  input  [31:0] row_31,
  output [31:0] row_0_2,
  output [31:0] row_1_2,
  output [31:0] row_2_2,
  output [31:0] row_3_2,
  output [31:0] row_4_2,
  output [31:0] row_5_2,
  output [31:0] row_6_2,
  output [31:0] row_7_2,
  output [31:0] row_8_2,
  output [31:0] row_9_2,
  output [31:0] row_10_2,
  output [31:0] row_11_2,
  output [31:0] row_12_2,
  output [31:0] row_13_2,
  output [31:0] row_14_2,
  output [31:0] row_15_2,
  output [31:0] row_16_2,
  output [31:0] row_17_2,
  output [31:0] row_18_2,
  output [31:0] row_19_2,
  output [31:0] row_20_2,
  output [31:0] row_21_2,
  output [31:0] row_22_2,
  output [31:0] row_23_2,
  output [31:0] row_24_2,
  output [31:0] row_25_2,
  output [31:0] row_26_2,
  output [31:0] row_27_2,
  output [31:0] row_28_2,
  output [31:0] row_29_2,
  output [31:0] row_30_2,
  output [31:0] row_31_2
);

  Register #(.width(32)) register_1 (.D(row_0), .Q(row_0_2), .clk(update));  // open: en, clr
  Register #(.width(32)) register_2 (.D(row_1), .Q(row_1_2), .clk(update));  // open: en, clr
  Register #(.width(32)) register_3 (.D(row_2), .Q(row_2_2), .clk(update));  // open: en, clr
  Register #(.width(32)) register_4 (.D(row_3), .Q(row_3_2), .clk(update));  // open: en, clr
  Register #(.width(32)) register_5 (.D(row_4), .Q(row_4_2), .clk(update));  // open: en, clr
  Register #(.width(32)) register_6 (.D(row_5), .Q(row_5_2), .clk(update));  // open: en, clr
  Register #(.width(32)) register_7 (.D(row_6), .Q(row_6_2), .clk(update));  // open: en, clr
  Register #(.width(32)) register_8 (.D(row_7), .Q(row_7_2), .clk(update));  // open: en, clr
  Register #(.width(32)) register_9 (.D(row_8), .Q(row_8_2), .clk(update));  // open: en, clr
  Register #(.width(32)) register_10 (.D(row_9), .Q(row_9_2), .clk(update));  // open: en, clr
  Register #(.width(32)) register_11 (.D(row_10), .Q(row_10_2), .clk(update));  // open: en, clr
  Register #(.width(32)) register_12 (.D(row_11), .Q(row_11_2), .clk(update));  // open: en, clr
  Register #(.width(32)) register_13 (.D(row_12), .Q(row_12_2), .clk(update));  // open: en, clr
  Register #(.width(32)) register_14 (.D(row_13), .Q(row_13_2), .clk(update));  // open: en, clr
  Register #(.width(32)) register_15 (.D(row_14), .Q(row_14_2), .clk(update));  // open: en, clr
  Register #(.width(32)) register_16 (.D(row_15), .Q(row_15_2), .clk(update));  // open: en, clr
  Register #(.width(32)) register_17 (.D(row_16), .Q(row_16_2), .clk(update));  // open: en, clr
  Register #(.width(32)) register_18 (.D(row_17), .Q(row_17_2), .clk(update));  // open: en, clr
  Register #(.width(32)) register_19 (.D(row_18), .Q(row_18_2), .clk(update));  // open: en, clr
  Register #(.width(32)) register_20 (.D(row_19), .Q(row_19_2), .clk(update));  // open: en, clr
  Register #(.width(32)) register_21 (.D(row_20), .Q(row_20_2), .clk(update));  // open: en, clr
  Register #(.width(32)) register_22 (.D(row_21), .Q(row_21_2), .clk(update));  // open: en, clr
  Register #(.width(32)) register_23 (.D(row_22), .Q(row_22_2), .clk(update));  // open: en, clr
  Register #(.width(32)) register_24 (.D(row_23), .Q(row_23_2), .clk(update));  // open: en, clr
  Register #(.width(32)) register_25 (.D(row_24), .Q(row_24_2), .clk(update));  // open: en, clr
  Register #(.width(32)) register_26 (.D(row_25), .Q(row_25_2), .clk(update));  // open: en, clr
  Register #(.width(32)) register_27 (.D(row_26), .Q(row_26_2), .clk(update));  // open: en, clr
  Register #(.width(32)) register_28 (.D(row_27), .Q(row_27_2), .clk(update));  // open: en, clr
  Register #(.width(32)) register_29 (.D(row_28), .Q(row_28_2), .clk(update));  // open: en, clr
  Register #(.width(32)) register_30 (.D(row_29), .Q(row_29_2), .clk(update));  // open: en, clr
  Register #(.width(32)) register_31 (.D(row_30), .Q(row_30_2), .clk(update));  // open: en, clr
  Register #(.width(32)) register_32 (.D(row_31), .Q(row_31_2), .clk(update));  // open: en, clr
endmodule

module cursor (
  input  [6:0] ASCII_code,
  output [4:0] X,
  output [4:0] Y,
  output is_enter
);

  wire comparator_1_eq, comparator_2_eq, comparator_3_eq, comparator_4_eq, or_1_out, or_2_out;
  wire [6:0] adder_1_out, adder_2_out, subtractor_1_out, subtractor_2_out, transistor_1_out, transistor_2_out;
  wire [6:5] X_out, Y_out;

  // Probe on ASCII_code
  Comparator #(.width(7)) comparator_1 (.a(ASCII_code), .b(7'b1100100), .eq(comparator_1_eq));  // open: gt, lt
  Comparator #(.width(7)) comparator_2 (.a(ASCII_code), .b(7'b1100001), .eq(comparator_2_eq));  // open: gt, lt
  Comparator #(.width(7)) comparator_3 (.a(ASCII_code), .b(7'b1110111), .eq(comparator_3_eq));  // open: gt, lt
  Comparator #(.width(7)) comparator_4 (.a(ASCII_code), .b(7'b1110011), .eq(comparator_4_eq));  // open: gt, lt
  Comparator #(.width(7)) comparator_5 (.a(ASCII_code), .b(7'b1100101), .eq(is_enter));  // open: gt, lt
  Adder #(.width(7)) adder_1 (.a(7'b0000001), .b({X_out, X}), .out(adder_1_out));  // open: cin, cout
  Subtractor #(.width(7)) subtractor_1 (.a({X_out, X}), .b(7'b0000001), .out(subtractor_1_out));  // open: bin, bout
  Adder #(.width(7)) adder_2 (.a(7'b0000001), .b({Y_out, Y}), .out(adder_2_out));  // open: cin, cout
  Subtractor #(.width(7)) subtractor_2 (.a({Y_out, Y}), .b(7'b0000001), .out(subtractor_2_out));  // open: bin, bout
  Transistor #(.\type ("n"), .width(7)) transistor_1 (
    .in(subtractor_1_out), .out(transistor_1_out), .gate(comparator_1_eq));
  Transistor #(.\type ("n"), .gate("br"), .width(7)) transistor_2 (
    .in(adder_2_out), .out(transistor_2_out), .gate(comparator_4_eq));
  or or_1 (or_1_out, comparator_1_eq, comparator_2_eq);
  Transistor #(.width(7)) transistor_3 (.in(adder_1_out), .out(transistor_1_out), .gate(comparator_1_eq));
  Transistor #(.gate("br"), .width(7)) transistor_4 (
    .in(subtractor_2_out), .out(transistor_2_out), .gate(comparator_4_eq));
  or or_2 (or_2_out, comparator_3_eq, comparator_4_eq);
  Register #(.width(7)) u_X (.D(transistor_1_out), .Q({X_out, X}), .clk(or_1_out));  // open: en, clr
  Register #(.width(7)) u_Y (.D(transistor_2_out), .Q({Y_out, Y}), .clk(or_2_out));  // open: en, clr

  // Other names for the same wires on the sheet: X_out[4:0] = X; Y_out[4:0] = Y

  // Notes on the sheet:
  //   =D
  //   =A
  //   =W
  //   =S
endmodule

module cursor_visualization (
  input  [4:0] Y,
  input  on_off,
  input  [4:0] X,
  input  [31:0] row_0,
  input  [31:0] row_1,
  input  [31:0] row_2,
  input  [31:0] row_3,
  input  [31:0] row_4,
  input  [31:0] row_5,
  input  [31:0] row_6,
  input  [31:0] row_7,
  input  [31:0] row_8,
  input  [31:0] row_9,
  input  [31:0] row_10,
  input  [31:0] row_11,
  input  [31:0] row_12,
  input  [31:0] row_13,
  input  [31:0] row_14,
  input  [31:0] row_15,
  input  [31:0] row_16,
  input  [31:0] row_17,
  input  [31:0] row_18,
  input  [31:0] row_19,
  input  [31:0] row_20,
  input  [31:0] row_21,
  input  [31:0] row_22,
  input  [31:0] row_23,
  input  [31:0] row_24,
  input  [31:0] row_25,
  input  [31:0] row_26,
  input  [31:0] row_27,
  input  [31:0] row_28,
  input  [31:0] row_29,
  input  [31:0] row_30,
  input  [31:0] row_31,
  output [31:0] row_0_2,
  output [31:0] row_1_2,
  output [31:0] row_2_2,
  output [31:0] row_3_2,
  output [31:0] row_4_2,
  output [31:0] row_5_2,
  output [31:0] row_6_2,
  output [31:0] row_7_2,
  output [31:0] row_8_2,
  output [31:0] row_9_2,
  output [31:0] row_10_2,
  output [31:0] row_11_2,
  output [31:0] row_12_2,
  output [31:0] row_13_2,
  output [31:0] row_14_2,
  output [31:0] row_15_2,
  output [31:0] row_16_2,
  output [31:0] row_17_2,
  output [31:0] row_18_2,
  output [31:0] row_19_2,
  output [31:0] row_20_2,
  output [31:0] row_21_2,
  output [31:0] row_22_2,
  output [31:0] row_23_2,
  output [31:0] row_24_2,
  output [31:0] row_25_2,
  output [31:0] row_26_2,
  output [31:0] row_27_2,
  output [31:0] row_28_2,
  output [31:0] row_29_2,
  output [31:0] row_30_2,
  output [31:0] row_31_2
);

  wire comparator_1_eq, comparator_2_eq, comparator_3_eq, comparator_4_eq, comparator_5_eq, comparator_6_eq,
       comparator_7_eq, comparator_8_eq, comparator_9_eq, comparator_10_eq, comparator_11_eq,
       comparator_12_eq, comparator_13_eq, comparator_14_eq, comparator_15_eq, comparator_16_eq,
       comparator_17_eq, comparator_18_eq, comparator_19_eq, comparator_20_eq, comparator_21_eq,
       comparator_22_eq, comparator_23_eq, comparator_24_eq, comparator_25_eq, comparator_26_eq,
       comparator_27_eq, comparator_28_eq, comparator_29_eq, comparator_30_eq, comparator_31_eq,
       comparator_32_eq, on, pull_resistor_4_node, pull_resistor_6_node, pull_resistor_7_node,
       pull_resistor_8_node, pull_resistor_10_node, pull_resistor_12_node, pull_resistor_14_node,
       pull_resistor_17_node, pull_resistor_18_node, pull_resistor_21_node, pull_resistor_24_node,
       pull_resistor_25_node, pull_resistor_26_node, pull_resistor_28_node, pull_resistor_29_node,
       pull_resistor_31_node, transistor_1_out, transistor_2_out, transistor_3_out, transistor_5_out,
       transistor_9_out, transistor_11_out, transistor_13_out, transistor_15_out, transistor_16_out,
       transistor_19_out, transistor_20_out, transistor_22_out, transistor_23_out, transistor_27_out,
       transistor_30_out, transistor_32_out;
  wire [31:0] multiplexer_1_out, new_row, shifter_1_out;

  Multiplexer #(.select(5), .width(32), .disabled(0), .enable("false")) multiplexer_1 (
    .in0(row_0), .in1(row_1), .in2(row_2), .in3(row_3), .in4(row_4), .in5(row_5), .in6(row_6), .in7(row_7),
    .in8(row_8), .in9(row_9), .in10(row_10), .in11(row_11), .in12(row_12), .in13(row_13), .in14(row_14),
    .in15(row_15), .in16(row_16), .in17(row_17), .in18(row_18), .in19(row_19), .in20(row_20), .in21(row_21),
    .in22(row_22), .in23(row_23), .in24(row_24), .in25(row_25), .in26(row_26), .in27(row_27), .in28(row_28),
    .in29(row_29), .in30(row_30), .in31(row_31), .out(multiplexer_1_out), .sel(Y));
  not not_1 (on, on_off);
  Shifter #(.width(32)) shifter_1 (.in(32'h1), .\dist (X), .out(shifter_1_out));
  assign new_row = shifter_1_out | multiplexer_1_out;  // OR_Gate or_1, 32 bits wide
  Comparator #(.width(5)) comparator_1 (.a({5{1'b0}}), .b(Y), .eq(comparator_1_eq));  // open: gt, lt
  Comparator #(.width(5)) comparator_2 (.a(5'b00001), .b(Y), .eq(comparator_2_eq));  // open: gt, lt
  Comparator #(.width(5)) comparator_3 (.a(5'b00010), .b(Y), .eq(comparator_3_eq));  // open: gt, lt
  Comparator #(.width(5)) comparator_4 (.a(5'b00011), .b(Y), .eq(comparator_4_eq));  // open: gt, lt
  Comparator #(.width(5)) comparator_5 (.a(5'b00100), .b(Y), .eq(comparator_5_eq));  // open: gt, lt
  Comparator #(.width(5)) comparator_6 (.a(5'b00101), .b(Y), .eq(comparator_6_eq));  // open: gt, lt
  Comparator #(.width(5)) comparator_7 (.a(5'b00110), .b(Y), .eq(comparator_7_eq));  // open: gt, lt
  Comparator #(.width(5)) comparator_8 (.a(5'b00111), .b(Y), .eq(comparator_8_eq));  // open: gt, lt
  Comparator #(.width(5)) comparator_9 (.a(5'b01000), .b(Y), .eq(comparator_9_eq));  // open: gt, lt
  Comparator #(.width(5)) comparator_10 (.a(5'b01001), .b(Y), .eq(comparator_10_eq));  // open: gt, lt
  Comparator #(.width(5)) comparator_11 (.a(5'b01010), .b(Y), .eq(comparator_11_eq));  // open: gt, lt
  Comparator #(.width(5)) comparator_12 (.a(5'b01011), .b(Y), .eq(comparator_12_eq));  // open: gt, lt
  Comparator #(.width(5)) comparator_13 (.a(5'b01100), .b(Y), .eq(comparator_13_eq));  // open: gt, lt
  Comparator #(.width(5)) comparator_14 (.a(5'b01101), .b(Y), .eq(comparator_14_eq));  // open: gt, lt
  Comparator #(.width(5)) comparator_15 (.a(5'b01110), .b(Y), .eq(comparator_15_eq));  // open: gt, lt
  Comparator #(.width(5)) comparator_16 (.a(5'b01111), .b(Y), .eq(comparator_16_eq));  // open: gt, lt
  Comparator #(.width(5)) comparator_17 (.a(5'b10000), .b(Y), .eq(comparator_17_eq));  // open: gt, lt
  Comparator #(.width(5)) comparator_18 (.a(5'b10001), .b(Y), .eq(comparator_18_eq));  // open: gt, lt
  Comparator #(.width(5)) comparator_19 (.a(5'b10010), .b(Y), .eq(comparator_19_eq));  // open: gt, lt
  Comparator #(.width(5)) comparator_20 (.a(5'b10011), .b(Y), .eq(comparator_20_eq));  // open: gt, lt
  Comparator #(.width(5)) comparator_21 (.a(5'b10100), .b(Y), .eq(comparator_21_eq));  // open: gt, lt
  Comparator #(.width(5)) comparator_22 (.a(5'b10101), .b(Y), .eq(comparator_22_eq));  // open: gt, lt
  Comparator #(.width(5)) comparator_23 (.a(5'b10110), .b(Y), .eq(comparator_23_eq));  // open: gt, lt
  Comparator #(.width(5)) comparator_24 (.a(5'b10111), .b(Y), .eq(comparator_24_eq));  // open: gt, lt
  Comparator #(.width(5)) comparator_25 (.a(5'b11000), .b(Y), .eq(comparator_25_eq));  // open: gt, lt
  Comparator #(.width(5)) comparator_26 (.a(5'b11001), .b(Y), .eq(comparator_26_eq));  // open: gt, lt
  Comparator #(.width(5)) comparator_27 (.a(5'b11010), .b(Y), .eq(comparator_27_eq));  // open: gt, lt
  Comparator #(.width(5)) comparator_28 (.a(5'b11011), .b(Y), .eq(comparator_28_eq));  // open: gt, lt
  Comparator #(.width(5)) comparator_29 (.a(5'b11100), .b(Y), .eq(comparator_29_eq));  // open: gt, lt
  Comparator #(.width(5)) comparator_30 (.a(5'b11101), .b(Y), .eq(comparator_30_eq));  // open: gt, lt
  Comparator #(.width(5)) comparator_31 (.a(5'b11110), .b(Y), .eq(comparator_31_eq));  // open: gt, lt
  Comparator #(.width(5)) comparator_32 (.a({5{1'b1}}), .b(Y), .eq(comparator_32_eq));  // open: gt, lt
  Transistor transistor_1 (.in(comparator_1_eq), .out(transistor_1_out), .gate(on));
  Pull_Resistor pull_resistor_1 (.node(transistor_1_out));
  Multiplexer #(.width(32), .disabled(0), .enable("false")) multiplexer_2 (
    .in0(row_0), .in1(new_row), .out(row_0_2), .sel(transistor_1_out));
  Transistor transistor_2 (.in(comparator_2_eq), .out(transistor_2_out), .gate(on));
  Pull_Resistor pull_resistor_2 (.node(transistor_2_out));
  Multiplexer #(.width(32), .disabled(0), .enable("false")) multiplexer_3 (
    .in0(row_1), .in1(new_row), .out(row_1_2), .sel(transistor_2_out));
  Transistor transistor_3 (.in(comparator_3_eq), .out(transistor_3_out), .gate(on));
  Pull_Resistor pull_resistor_3 (.node(transistor_3_out));
  Multiplexer #(.width(32), .disabled(0), .enable("false")) multiplexer_4 (
    .in0(row_2), .in1(new_row), .out(row_2_2), .sel(transistor_3_out));
  Pull_Resistor pull_resistor_4 (.node(pull_resistor_4_node));
  Transistor transistor_4 (.in(comparator_4_eq), .out(pull_resistor_4_node), .gate(on));
  Multiplexer #(.width(32), .disabled(0), .enable("false")) multiplexer_5 (
    .in0(row_3), .in1(new_row), .out(row_3_2), .sel(pull_resistor_4_node));
  Transistor transistor_5 (.in(comparator_5_eq), .out(transistor_5_out), .gate(on));
  Pull_Resistor pull_resistor_5 (.node(transistor_5_out));
  Multiplexer #(.width(32), .disabled(0), .enable("false")) multiplexer_6 (
    .in0(row_4), .in1(new_row), .out(row_4_2), .sel(transistor_5_out));
  Pull_Resistor pull_resistor_6 (.node(pull_resistor_6_node));
  Transistor transistor_6 (.in(comparator_6_eq), .out(pull_resistor_6_node), .gate(on));
  Multiplexer #(.width(32), .disabled(0), .enable("false")) multiplexer_7 (
    .in0(row_5), .in1(new_row), .out(row_5_2), .sel(pull_resistor_6_node));
  Pull_Resistor pull_resistor_7 (.node(pull_resistor_7_node));
  Transistor transistor_7 (.in(comparator_7_eq), .out(pull_resistor_7_node), .gate(on));
  Multiplexer #(.width(32), .disabled(0), .enable("false")) multiplexer_8 (
    .in0(row_6), .in1(new_row), .out(row_6_2), .sel(pull_resistor_7_node));
  Pull_Resistor pull_resistor_8 (.node(pull_resistor_8_node));
  Transistor transistor_8 (.in(comparator_8_eq), .out(pull_resistor_8_node), .gate(on));
  Multiplexer #(.width(32), .disabled(0), .enable("false")) multiplexer_9 (
    .in0(row_7), .in1(new_row), .out(row_7_2), .sel(pull_resistor_8_node));
  Transistor transistor_9 (.in(comparator_9_eq), .out(transistor_9_out), .gate(on));
  Pull_Resistor pull_resistor_9 (.node(transistor_9_out));
  Multiplexer #(.width(32), .disabled(0), .enable("false")) multiplexer_10 (
    .in0(row_8), .in1(new_row), .out(row_8_2), .sel(transistor_9_out));
  Pull_Resistor pull_resistor_10 (.node(pull_resistor_10_node));
  Transistor transistor_10 (.in(comparator_10_eq), .out(pull_resistor_10_node), .gate(on));
  Multiplexer #(.width(32), .disabled(0), .enable("false")) multiplexer_11 (
    .in0(row_9), .in1(new_row), .out(row_9_2), .sel(pull_resistor_10_node));
  Transistor transistor_11 (.in(comparator_11_eq), .out(transistor_11_out), .gate(on));
  Pull_Resistor pull_resistor_11 (.node(transistor_11_out));
  Multiplexer #(.width(32), .disabled(0), .enable("false")) multiplexer_12 (
    .in0(row_10), .in1(new_row), .out(row_10_2), .sel(transistor_11_out));
  Pull_Resistor pull_resistor_12 (.node(pull_resistor_12_node));
  Transistor transistor_12 (.in(comparator_12_eq), .out(pull_resistor_12_node), .gate(on));
  Multiplexer #(.width(32), .disabled(0), .enable("false")) multiplexer_13 (
    .in0(row_11), .in1(new_row), .out(row_11_2), .sel(pull_resistor_12_node));
  Transistor transistor_13 (.in(comparator_13_eq), .out(transistor_13_out), .gate(on));
  Pull_Resistor pull_resistor_13 (.node(transistor_13_out));
  Multiplexer #(.width(32), .disabled(0), .enable("false")) multiplexer_14 (
    .in0(row_12), .in1(new_row), .out(row_12_2), .sel(transistor_13_out));
  Pull_Resistor pull_resistor_14 (.node(pull_resistor_14_node));
  Transistor transistor_14 (.in(comparator_14_eq), .out(pull_resistor_14_node), .gate(on));
  Multiplexer #(.width(32), .disabled(0), .enable("false")) multiplexer_15 (
    .in0(row_13), .in1(new_row), .out(row_13_2), .sel(pull_resistor_14_node));
  Transistor transistor_15 (.in(comparator_15_eq), .out(transistor_15_out), .gate(on));
  Pull_Resistor pull_resistor_15 (.node(transistor_15_out));
  Multiplexer #(.width(32), .disabled(0), .enable("false")) multiplexer_16 (
    .in0(row_14), .in1(new_row), .out(row_14_2), .sel(transistor_15_out));
  Transistor transistor_16 (.in(comparator_16_eq), .out(transistor_16_out), .gate(on));
  Pull_Resistor pull_resistor_16 (.node(transistor_16_out));
  Multiplexer #(.width(32), .disabled(0), .enable("false")) multiplexer_17 (
    .in0(row_15), .in1(new_row), .out(row_15_2), .sel(transistor_16_out));
  Pull_Resistor pull_resistor_17 (.node(pull_resistor_17_node));
  Transistor transistor_17 (.in(comparator_17_eq), .out(pull_resistor_17_node), .gate(on));
  Multiplexer #(.width(32), .disabled(0), .enable("false")) multiplexer_18 (
    .in0(row_16), .in1(new_row), .out(row_16_2), .sel(pull_resistor_17_node));
  Pull_Resistor pull_resistor_18 (.node(pull_resistor_18_node));
  Transistor transistor_18 (.in(comparator_18_eq), .out(pull_resistor_18_node), .gate(on));
  Multiplexer #(.width(32), .disabled(0), .enable("false")) multiplexer_19 (
    .in0(row_17), .in1(new_row), .out(row_17_2), .sel(pull_resistor_18_node));
  Transistor transistor_19 (.in(comparator_19_eq), .out(transistor_19_out), .gate(on));
  Pull_Resistor pull_resistor_19 (.node(transistor_19_out));
  Multiplexer #(.width(32), .disabled(0), .enable("false")) multiplexer_20 (
    .in0(row_18), .in1(new_row), .out(row_18_2), .sel(transistor_19_out));
  Transistor transistor_20 (.in(comparator_20_eq), .out(transistor_20_out), .gate(on));
  Pull_Resistor pull_resistor_20 (.node(transistor_20_out));
  Multiplexer #(.width(32), .disabled(0), .enable("false")) multiplexer_21 (
    .in0(row_19), .in1(new_row), .out(row_19_2), .sel(transistor_20_out));
  Pull_Resistor pull_resistor_21 (.node(pull_resistor_21_node));
  Transistor transistor_21 (.in(comparator_21_eq), .out(pull_resistor_21_node), .gate(on));
  Multiplexer #(.width(32), .disabled(0), .enable("false")) multiplexer_22 (
    .in0(row_20), .in1(new_row), .out(row_20_2), .sel(pull_resistor_21_node));
  Transistor transistor_22 (.in(comparator_22_eq), .out(transistor_22_out), .gate(on));
  Pull_Resistor pull_resistor_22 (.node(transistor_22_out));
  Multiplexer #(.width(32), .disabled(0), .enable("false")) multiplexer_23 (
    .in0(row_21), .in1(new_row), .out(row_21_2), .sel(transistor_22_out));
  Transistor transistor_23 (.in(comparator_23_eq), .out(transistor_23_out), .gate(on));
  Pull_Resistor pull_resistor_23 (.node(transistor_23_out));
  Multiplexer #(.width(32), .disabled(0), .enable("false")) multiplexer_24 (
    .in0(row_22), .in1(new_row), .out(row_22_2), .sel(transistor_23_out));
  Pull_Resistor pull_resistor_24 (.node(pull_resistor_24_node));
  Transistor transistor_24 (.in(comparator_24_eq), .out(pull_resistor_24_node), .gate(on));
  Multiplexer #(.width(32), .disabled(0), .enable("false")) multiplexer_25 (
    .in0(row_23), .in1(new_row), .out(row_23_2), .sel(pull_resistor_24_node));
  Pull_Resistor pull_resistor_25 (.node(pull_resistor_25_node));
  Transistor transistor_25 (.in(comparator_25_eq), .out(pull_resistor_25_node), .gate(on));
  Multiplexer #(.width(32), .disabled(0), .enable("false")) multiplexer_26 (
    .in0(row_24), .in1(new_row), .out(row_24_2), .sel(pull_resistor_25_node));
  Pull_Resistor pull_resistor_26 (.node(pull_resistor_26_node));
  Transistor transistor_26 (.in(comparator_26_eq), .out(pull_resistor_26_node), .gate(on));
  Multiplexer #(.width(32), .disabled(0), .enable("false")) multiplexer_27 (
    .in0(row_25), .in1(new_row), .out(row_25_2), .sel(pull_resistor_26_node));
  Transistor transistor_27 (.in(comparator_27_eq), .out(transistor_27_out), .gate(on));
  Pull_Resistor pull_resistor_27 (.node(transistor_27_out));
  Multiplexer #(.width(32), .disabled(0), .enable("false")) multiplexer_28 (
    .in0(row_26), .in1(new_row), .out(row_26_2), .sel(transistor_27_out));
  Pull_Resistor pull_resistor_28 (.node(pull_resistor_28_node));
  Transistor transistor_28 (.in(comparator_28_eq), .out(pull_resistor_28_node), .gate(on));
  Multiplexer #(.width(32), .disabled(0), .enable("false")) multiplexer_29 (
    .in0(row_27), .in1(new_row), .out(row_27_2), .sel(pull_resistor_28_node));
  Pull_Resistor pull_resistor_29 (.node(pull_resistor_29_node));
  Transistor transistor_29 (.in(comparator_29_eq), .out(pull_resistor_29_node), .gate(on));
  Multiplexer #(.width(32), .disabled(0), .enable("false")) multiplexer_30 (
    .in0(row_28), .in1(new_row), .out(row_28_2), .sel(pull_resistor_29_node));
  Transistor transistor_30 (.in(comparator_30_eq), .out(transistor_30_out), .gate(on));
  Pull_Resistor pull_resistor_30 (.node(transistor_30_out));
  Multiplexer #(.width(32), .disabled(0), .enable("false")) multiplexer_31 (
    .in0(row_29), .in1(new_row), .out(row_29_2), .sel(transistor_30_out));
  Pull_Resistor pull_resistor_31 (.node(pull_resistor_31_node));
  Transistor transistor_31 (.in(comparator_31_eq), .out(pull_resistor_31_node), .gate(on));
  Multiplexer #(.width(32), .disabled(0), .enable("false")) multiplexer_32 (
    .in0(row_30), .in1(new_row), .out(row_30_2), .sel(pull_resistor_31_node));
  Transistor transistor_32 (.in(comparator_32_eq), .out(transistor_32_out), .gate(on));
  Pull_Resistor pull_resistor_32 (.node(transistor_32_out));
  Multiplexer #(.width(32), .disabled(0), .enable("false")) multiplexer_33 (
    .in0(row_31), .in1(new_row), .out(row_31_2), .sel(transistor_32_out));

  // Other names for the same wires on the sheet: _0[31:0] = row_0; _1[31:0] = row_1; _2[31:0] = row_2;
  //   _3[31:0] = row_3; _4[31:0] = row_4; _5[31:0] = row_5; _6[31:0] = row_6; _7[31:0] = row_7; _8[31:0] = row_8;
  //   _9[31:0] = row_9; _10[31:0] = row_10; _11[31:0] = row_11; _12[31:0] = row_12; _13[31:0] = row_13;
  //   _14[31:0] = row_14; _15[31:0] = row_15; _16[31:0] = row_16; _17[31:0] = row_17; _18[31:0] = row_18;
  //   _19[31:0] = row_19; _20[31:0] = row_20; _21[31:0] = row_21; _22[31:0] = row_22; _23[31:0] = row_23;
  //   _24[31:0] = row_24; _25[31:0] = row_25; _26[31:0] = row_26; _27[31:0] = row_27; _28[31:0] = row_28;
  //   _29[31:0] = row_29; _30[31:0] = row_30; _31[31:0] = row_31
endmodule
module zone_visualization (
  input  [3:0] Number_of_dead_zones,
  input  [31:0] row_0,
  input  [31:0] row_1,
  input  [31:0] row_2,
  input  [31:0] row_3,
  input  [31:0] row_4,
  input  [31:0] row_5,
  input  [31:0] row_6,
  input  [31:0] row_7,
  input  [31:0] row_8,
  input  [31:0] row_9,
  input  [31:0] row_10,
  input  [31:0] row_11,
  input  [31:0] row_12,
  input  [31:0] row_13,
  input  [31:0] row_14,
  input  [31:0] row_15,
  input  [31:0] row_16,
  input  [31:0] row_17,
  input  [31:0] row_18,
  input  [31:0] row_19,
  input  [31:0] row_20,
  input  [31:0] row_21,
  input  [31:0] row_22,
  input  [31:0] row_23,
  input  [31:0] row_24,
  input  [31:0] row_25,
  input  [31:0] row_26,
  input  [31:0] row_27,
  input  [31:0] row_28,
  input  [31:0] row_29,
  input  [31:0] row_30,
  input  [31:0] row_31,
  output [31:0] row_0_2,
  output [31:0] row_1_2,
  output [31:0] row_2_2,
  output [31:0] row_3_2,
  output [31:0] row_4_2,
  output [31:0] row_5_2,
  output [31:0] row_6_2,
  output [31:0] row_7_2,
  output [31:0] row_8_2,
  output [31:0] row_9_2,
  output [31:0] row_10_2,
  output [31:0] row_11_2,
  output [31:0] row_12_2,
  output [31:0] row_13_2,
  output [31:0] row_14_2,
  output [31:0] row_15_2,
  output [31:0] row_16_2,
  output [31:0] row_17_2,
  output [31:0] row_18_2,
  output [31:0] row_19_2,
  output [31:0] row_20_2,
  output [31:0] row_21_2,
  output [31:0] row_22_2,
  output [31:0] row_23_2,
  output [31:0] row_24_2,
  output [31:0] row_25_2,
  output [31:0] row_26_2,
  output [31:0] row_27_2,
  output [31:0] row_28_2,
  output [31:0] row_29_2,
  output [31:0] row_30_2,
  output [31:0] row_31_2
);

  wire comparator_1_eq, comparator_1_lt, comparator_2_eq, comparator_2_lt, comparator_3_eq, comparator_3_lt,
       comparator_4_eq, comparator_4_lt, comparator_5_eq, comparator_5_lt, comparator_6_eq, comparator_6_lt,
       comparator_7_eq, comparator_7_lt, comparator_8_eq, comparator_8_lt, comparator_9_eq, comparator_9_lt,
       comparator_10_eq, comparator_10_lt, comparator_11_eq, comparator_11_lt, comparator_12_eq,
       comparator_12_lt, comparator_13_eq, comparator_13_lt, comparator_14_eq, comparator_14_lt,
       comparator_15_eq, comparator_15_lt, comparator_16_eq, comparator_16_gt, comparator_17_eq,
       comparator_17_gt, comparator_18_eq, comparator_18_gt, comparator_19_eq, comparator_19_gt,
       comparator_20_eq, comparator_20_gt, comparator_21_eq, comparator_21_gt, comparator_22_eq,
       comparator_22_gt, comparator_23_eq, comparator_23_gt, comparator_24_eq, comparator_24_gt,
       comparator_25_eq, comparator_25_gt, comparator_26_eq, comparator_26_gt, comparator_27_eq,
       comparator_27_gt, comparator_28_eq, comparator_28_gt, comparator_29_eq, comparator_29_gt,
       comparator_30_eq, comparator_30_gt, or_33_out, or_35_out, or_37_out, or_39_out, or_41_out, or_43_out,
       or_45_out, or_47_out, or_49_out, or_51_out, or_53_out, or_55_out, or_57_out, or_59_out, or_61_out,
       or_78_out, or_79_out, or_80_out, or_81_out, or_82_out, or_83_out, or_84_out, or_85_out, or_86_out,
       or_87_out, or_88_out, or_89_out, or_90_out, or_91_out, or_92_out;
  wire [31:0] _0, _1, _2, _3, _4, _5, _6, _7, _8, _9, _10, _11, _12, _13, _14, _17, _18, _19, _20, _21, _22,
       _23, _24, _25, _26, _27, _28, _29, _30, _31, border, border2, multiplexer_1_out, or_34_out, or_36_out,
       or_38_out, or_40_out, or_42_out, or_44_out, or_46_out, or_48_out, or_50_out, or_52_out, or_54_out,
       or_56_out, or_58_out, or_60_out, or_62_out, or_63_out, or_64_out, or_65_out, or_66_out, or_67_out,
       or_68_out, or_69_out, or_70_out, or_71_out, or_72_out, or_73_out, or_74_out, or_75_out, or_76_out,
       or_77_out;

  assign border = {{28{1'b0}}, Number_of_dead_zones};  // Bit_Extender bit_extender_1
  // Probe on border
  Multiplexer #(.select(4), .width(32), .disabled(0), .enable("false")) multiplexer_1 (
    .in0({32{1'b0}}), .in1(32'h80000001), .in2(32'hc0000003), .in3(32'he0000007), .in4(32'hf000000f),
    .in5(32'hf800001f), .in6(32'hfc00003f), .in7(32'hfe00007f), .in8(32'hff0000ff), .in9(32'hff8001ff),
    .in10(32'hffc003ff), .in11(32'hffe007ff), .in12(32'hfff00fff), .in13(32'hfff81fff), .in14(32'hfffc3fff),
    .in15(32'hfffe7fff), .out(multiplexer_1_out), .sel(Number_of_dead_zones));
  Subtractor #(.width(32)) subtractor_1 (.a(32'h21), .b(border), .out(border2));  // open: bin, bout
  // Probe on border2
  assign _0 = multiplexer_1_out | row_0;  // OR_Gate or_1, 32 bits wide
  assign _1 = multiplexer_1_out | row_1;  // OR_Gate or_2, 32 bits wide
  assign _2 = multiplexer_1_out | row_2;  // OR_Gate or_3, 32 bits wide
  assign _3 = multiplexer_1_out | row_3;  // OR_Gate or_4, 32 bits wide
  assign _4 = multiplexer_1_out | row_4;  // OR_Gate or_5, 32 bits wide
  assign _5 = multiplexer_1_out | row_5;  // OR_Gate or_6, 32 bits wide
  assign _6 = multiplexer_1_out | row_6;  // OR_Gate or_7, 32 bits wide
  assign _7 = multiplexer_1_out | row_7;  // OR_Gate or_8, 32 bits wide
  assign _8 = multiplexer_1_out | row_8;  // OR_Gate or_9, 32 bits wide
  assign _9 = multiplexer_1_out | row_9;  // OR_Gate or_10, 32 bits wide
  assign _10 = multiplexer_1_out | row_10;  // OR_Gate or_11, 32 bits wide
  assign _11 = multiplexer_1_out | row_11;  // OR_Gate or_12, 32 bits wide
  assign _12 = multiplexer_1_out | row_12;  // OR_Gate or_13, 32 bits wide
  assign _13 = multiplexer_1_out | row_13;  // OR_Gate or_14, 32 bits wide
  assign _14 = multiplexer_1_out | row_14;  // OR_Gate or_15, 32 bits wide
  assign row_15_2 = multiplexer_1_out | row_15;  // OR_Gate or_16, 32 bits wide
  assign row_16_2 = multiplexer_1_out | row_16;  // OR_Gate or_17, 32 bits wide
  assign _17 = multiplexer_1_out | row_17;  // OR_Gate or_18, 32 bits wide
  assign _18 = multiplexer_1_out | row_18;  // OR_Gate or_19, 32 bits wide
  assign _19 = multiplexer_1_out | row_19;  // OR_Gate or_20, 32 bits wide
  assign _20 = multiplexer_1_out | row_20;  // OR_Gate or_21, 32 bits wide
  assign _21 = multiplexer_1_out | row_21;  // OR_Gate or_22, 32 bits wide
  assign _22 = multiplexer_1_out | row_22;  // OR_Gate or_23, 32 bits wide
  assign _23 = multiplexer_1_out | row_23;  // OR_Gate or_24, 32 bits wide
  assign _24 = multiplexer_1_out | row_24;  // OR_Gate or_25, 32 bits wide
  assign _25 = multiplexer_1_out | row_25;  // OR_Gate or_26, 32 bits wide
  assign _26 = multiplexer_1_out | row_26;  // OR_Gate or_27, 32 bits wide
  assign _27 = multiplexer_1_out | row_27;  // OR_Gate or_28, 32 bits wide
  assign _28 = multiplexer_1_out | row_28;  // OR_Gate or_29, 32 bits wide
  assign _29 = multiplexer_1_out | row_29;  // OR_Gate or_30, 32 bits wide
  assign _30 = multiplexer_1_out | row_30;  // OR_Gate or_31, 32 bits wide
  assign _31 = multiplexer_1_out | row_31;  // OR_Gate or_32, 32 bits wide
  Comparator #(.width(32)) comparator_1 (
    .a(32'h1), .b(border), .eq(comparator_1_eq), .lt(comparator_1_lt));  // open: gt
  or or_33 (or_33_out, comparator_1_eq, comparator_1_lt);
  assign or_34_out = _0 | {32{1'b1}};  // OR_Gate or_34, 32 bits wide
  Comparator #(.width(32)) comparator_2 (
    .a(32'h2), .b(border), .eq(comparator_2_eq), .lt(comparator_2_lt));  // open: gt
  or or_35 (or_35_out, comparator_2_eq, comparator_2_lt);
  assign or_36_out = _1 | {32{1'b1}};  // OR_Gate or_36, 32 bits wide
  Comparator #(.width(32)) comparator_3 (
    .a(32'h3), .b(border), .eq(comparator_3_eq), .lt(comparator_3_lt));  // open: gt
  or or_37 (or_37_out, comparator_3_eq, comparator_3_lt);
  assign or_38_out = _2 | {32{1'b1}};  // OR_Gate or_38, 32 bits wide
  Comparator #(.width(32)) comparator_4 (
    .a(32'h4), .b(border), .eq(comparator_4_eq), .lt(comparator_4_lt));  // open: gt
  or or_39 (or_39_out, comparator_4_eq, comparator_4_lt);
  assign or_40_out = _3 | {32{1'b1}};  // OR_Gate or_40, 32 bits wide
  Comparator #(.width(32)) comparator_5 (
    .a(32'h5), .b(border), .eq(comparator_5_eq), .lt(comparator_5_lt));  // open: gt
  or or_41 (or_41_out, comparator_5_eq, comparator_5_lt);
  assign or_42_out = _4 | {32{1'b1}};  // OR_Gate or_42, 32 bits wide
  Comparator #(.width(32)) comparator_6 (
    .a(32'h6), .b(border), .eq(comparator_6_eq), .lt(comparator_6_lt));  // open: gt
  or or_43 (or_43_out, comparator_6_eq, comparator_6_lt);
  assign or_44_out = _5 | {32{1'b1}};  // OR_Gate or_44, 32 bits wide
  Comparator #(.width(32)) comparator_7 (
    .a(32'h7), .b(border), .eq(comparator_7_eq), .lt(comparator_7_lt));  // open: gt
  or or_45 (or_45_out, comparator_7_eq, comparator_7_lt);
  assign or_46_out = _6 | {32{1'b1}};  // OR_Gate or_46, 32 bits wide
  Comparator #(.width(32)) comparator_8 (
    .a(32'h8), .b(border), .eq(comparator_8_eq), .lt(comparator_8_lt));  // open: gt
  or or_47 (or_47_out, comparator_8_eq, comparator_8_lt);
  assign or_48_out = _7 | {32{1'b1}};  // OR_Gate or_48, 32 bits wide
  Comparator #(.width(32)) comparator_9 (
    .a(32'h9), .b(border), .eq(comparator_9_eq), .lt(comparator_9_lt));  // open: gt
  or or_49 (or_49_out, comparator_9_eq, comparator_9_lt);
  assign or_50_out = _8 | {32{1'b1}};  // OR_Gate or_50, 32 bits wide
  Comparator #(.width(32)) comparator_10 (
    .a(32'ha), .b(border), .eq(comparator_10_eq), .lt(comparator_10_lt));  // open: gt
  or or_51 (or_51_out, comparator_10_eq, comparator_10_lt);
  assign or_52_out = _9 | {32{1'b1}};  // OR_Gate or_52, 32 bits wide
  Comparator #(.width(32)) comparator_11 (
    .a(32'hb), .b(border), .eq(comparator_11_eq), .lt(comparator_11_lt));  // open: gt
  or or_53 (or_53_out, comparator_11_eq, comparator_11_lt);
  assign or_54_out = _10 | {32{1'b1}};  // OR_Gate or_54, 32 bits wide
  Comparator #(.width(32)) comparator_12 (
    .a(32'hc), .b(border), .eq(comparator_12_eq), .lt(comparator_12_lt));  // open: gt
  or or_55 (or_55_out, comparator_12_eq, comparator_12_lt);
  assign or_56_out = _11 | {32{1'b1}};  // OR_Gate or_56, 32 bits wide
  Comparator #(.width(32)) comparator_13 (
    .a(32'hd), .b(border), .eq(comparator_13_eq), .lt(comparator_13_lt));  // open: gt
  or or_57 (or_57_out, comparator_13_eq, comparator_13_lt);
  assign or_58_out = _12 | {32{1'b1}};  // OR_Gate or_58, 32 bits wide
  Comparator #(.width(32)) comparator_14 (
    .a(32'he), .b(border), .eq(comparator_14_eq), .lt(comparator_14_lt));  // open: gt
  or or_59 (or_59_out, comparator_14_eq, comparator_14_lt);
  assign or_60_out = _13 | {32{1'b1}};  // OR_Gate or_60, 32 bits wide
  Comparator #(.width(32)) comparator_15 (
    .a(32'hf), .b(border), .eq(comparator_15_eq), .lt(comparator_15_lt));  // open: gt
  or or_61 (or_61_out, comparator_15_eq, comparator_15_lt);
  assign or_62_out = _14 | {32{1'b1}};  // OR_Gate or_62, 32 bits wide
  Comparator #(.width(32)) comparator_16 (
    .a(32'h12), .b(border2), .gt(comparator_16_gt), .eq(comparator_16_eq));  // open: lt
  assign or_63_out = _17 | {32{1'b1}};  // OR_Gate or_63, 32 bits wide
  Comparator #(.width(32)) comparator_17 (
    .a(32'h13), .b(border2), .gt(comparator_17_gt), .eq(comparator_17_eq));  // open: lt
  assign or_64_out = _18 | {32{1'b1}};  // OR_Gate or_64, 32 bits wide
  Comparator #(.width(32)) comparator_18 (
    .a(32'h14), .b(border2), .gt(comparator_18_gt), .eq(comparator_18_eq));  // open: lt
  assign or_65_out = _19 | {32{1'b1}};  // OR_Gate or_65, 32 bits wide
  Comparator #(.width(32)) comparator_19 (
    .a(32'h15), .b(border2), .gt(comparator_19_gt), .eq(comparator_19_eq));  // open: lt
  assign or_66_out = _20 | {32{1'b1}};  // OR_Gate or_66, 32 bits wide
  Comparator #(.width(32)) comparator_20 (
    .a(32'h16), .b(border2), .gt(comparator_20_gt), .eq(comparator_20_eq));  // open: lt
  assign or_67_out = _21 | {32{1'b1}};  // OR_Gate or_67, 32 bits wide
  Comparator #(.width(32)) comparator_21 (
    .a(32'h17), .b(border2), .gt(comparator_21_gt), .eq(comparator_21_eq));  // open: lt
  assign or_68_out = _22 | {32{1'b1}};  // OR_Gate or_68, 32 bits wide
  Comparator #(.width(32)) comparator_22 (
    .a(32'h18), .b(border2), .gt(comparator_22_gt), .eq(comparator_22_eq));  // open: lt
  assign or_69_out = _23 | {32{1'b1}};  // OR_Gate or_69, 32 bits wide
  Comparator #(.width(32)) comparator_23 (
    .a(32'h19), .b(border2), .gt(comparator_23_gt), .eq(comparator_23_eq));  // open: lt
  assign or_70_out = _24 | {32{1'b1}};  // OR_Gate or_70, 32 bits wide
  Comparator #(.width(32)) comparator_24 (
    .a(32'h1a), .b(border2), .gt(comparator_24_gt), .eq(comparator_24_eq));  // open: lt
  assign or_71_out = _25 | {32{1'b1}};  // OR_Gate or_71, 32 bits wide
  Comparator #(.width(32)) comparator_25 (
    .a(32'h1b), .b(border2), .gt(comparator_25_gt), .eq(comparator_25_eq));  // open: lt
  assign or_72_out = _26 | {32{1'b1}};  // OR_Gate or_72, 32 bits wide
  Comparator #(.width(32)) comparator_26 (
    .a(32'h1c), .b(border2), .gt(comparator_26_gt), .eq(comparator_26_eq));  // open: lt
  assign or_73_out = _27 | {32{1'b1}};  // OR_Gate or_73, 32 bits wide
  Comparator #(.width(32)) comparator_27 (
    .a(32'h1d), .b(border2), .gt(comparator_27_gt), .eq(comparator_27_eq));  // open: lt
  assign or_74_out = _28 | {32{1'b1}};  // OR_Gate or_74, 32 bits wide
  Comparator #(.width(32)) comparator_28 (
    .a(32'h1e), .b(border2), .gt(comparator_28_gt), .eq(comparator_28_eq));  // open: lt
  assign or_75_out = _29 | {32{1'b1}};  // OR_Gate or_75, 32 bits wide
  Comparator #(.width(32)) comparator_29 (
    .a(32'h1f), .b(border2), .gt(comparator_29_gt), .eq(comparator_29_eq));  // open: lt
  assign or_76_out = _30 | {32{1'b1}};  // OR_Gate or_76, 32 bits wide
  Comparator #(.width(32)) comparator_30 (
    .a(32'h20), .b(border2), .gt(comparator_30_gt), .eq(comparator_30_eq));  // open: lt
  assign or_77_out = _31 | {32{1'b1}};  // OR_Gate or_77, 32 bits wide
  Multiplexer #(.width(32), .disabled(0), .enable("false")) multiplexer_2 (
    .in0(_0), .in1(or_34_out), .out(row_0_2), .sel(or_33_out));
  Multiplexer #(.width(32), .disabled(0), .enable("false")) multiplexer_3 (
    .in0(_1), .in1(or_36_out), .out(row_1_2), .sel(or_35_out));
  Multiplexer #(.width(32), .disabled(0), .enable("false")) multiplexer_4 (
    .in0(_2), .in1(or_38_out), .out(row_2_2), .sel(or_37_out));
  Multiplexer #(.width(32), .disabled(0), .enable("false")) multiplexer_5 (
    .in0(_3), .in1(or_40_out), .out(row_3_2), .sel(or_39_out));
  Multiplexer #(.width(32), .disabled(0), .enable("false")) multiplexer_6 (
    .in0(_4), .in1(or_42_out), .out(row_4_2), .sel(or_41_out));
  Multiplexer #(.width(32), .disabled(0), .enable("false")) multiplexer_7 (
    .in0(_5), .in1(or_44_out), .out(row_5_2), .sel(or_43_out));
  Multiplexer #(.width(32), .disabled(0), .enable("false")) multiplexer_8 (
    .in0(_6), .in1(or_46_out), .out(row_6_2), .sel(or_45_out));
  Multiplexer #(.width(32), .disabled(0), .enable("false")) multiplexer_9 (
    .in0(_7), .in1(or_48_out), .out(row_7_2), .sel(or_47_out));
  Multiplexer #(.width(32), .disabled(0), .enable("false")) multiplexer_10 (
    .in0(_8), .in1(or_50_out), .out(row_8_2), .sel(or_49_out));
  Multiplexer #(.width(32), .disabled(0), .enable("false")) multiplexer_11 (
    .in0(_9), .in1(or_52_out), .out(row_9_2), .sel(or_51_out));
  Multiplexer #(.width(32), .disabled(0), .enable("false")) multiplexer_12 (
    .in0(_10), .in1(or_54_out), .out(row_10_2), .sel(or_53_out));
  Multiplexer #(.width(32), .disabled(0), .enable("false")) multiplexer_13 (
    .in0(_11), .in1(or_56_out), .out(row_11_2), .sel(or_55_out));
  Multiplexer #(.width(32), .disabled(0), .enable("false")) multiplexer_14 (
    .in0(_12), .in1(or_58_out), .out(row_12_2), .sel(or_57_out));
  Multiplexer #(.width(32), .disabled(0), .enable("false")) multiplexer_15 (
    .in0(_13), .in1(or_60_out), .out(row_13_2), .sel(or_59_out));
  Multiplexer #(.width(32), .disabled(0), .enable("false")) multiplexer_16 (
    .in0(_14), .in1(or_62_out), .out(row_14_2), .sel(or_61_out));
  or or_78 (or_78_out, comparator_16_gt, comparator_16_eq);
  Multiplexer #(.width(32), .disabled(0), .enable("false")) multiplexer_17 (
    .in0(_17), .in1(or_63_out), .out(row_17_2), .sel(or_78_out));
  or or_79 (or_79_out, comparator_17_gt, comparator_17_eq);
  Multiplexer #(.width(32), .disabled(0), .enable("false")) multiplexer_18 (
    .in0(_18), .in1(or_64_out), .out(row_18_2), .sel(or_79_out));
  or or_80 (or_80_out, comparator_18_gt, comparator_18_eq);
  Multiplexer #(.width(32), .disabled(0), .enable("false")) multiplexer_19 (
    .in0(_19), .in1(or_65_out), .out(row_19_2), .sel(or_80_out));
  or or_81 (or_81_out, comparator_19_gt, comparator_19_eq);
  Multiplexer #(.width(32), .disabled(0), .enable("false")) multiplexer_20 (
    .in0(_20), .in1(or_66_out), .out(row_20_2), .sel(or_81_out));
  or or_82 (or_82_out, comparator_20_gt, comparator_20_eq);
  Multiplexer #(.width(32), .disabled(0), .enable("false")) multiplexer_21 (
    .in0(_21), .in1(or_67_out), .out(row_21_2), .sel(or_82_out));
  or or_83 (or_83_out, comparator_21_gt, comparator_21_eq);
  Multiplexer #(.width(32), .disabled(0), .enable("false")) multiplexer_22 (
    .in0(_22), .in1(or_68_out), .out(row_22_2), .sel(or_83_out));
  or or_84 (or_84_out, comparator_22_gt, comparator_22_eq);
  Multiplexer #(.width(32), .disabled(0), .enable("false")) multiplexer_23 (
    .in0(_23), .in1(or_69_out), .out(row_23_2), .sel(or_84_out));
  or or_85 (or_85_out, comparator_23_gt, comparator_23_eq);
  Multiplexer #(.width(32), .disabled(0), .enable("false")) multiplexer_24 (
    .in0(_24), .in1(or_70_out), .out(row_24_2), .sel(or_85_out));
  or or_86 (or_86_out, comparator_24_gt, comparator_24_eq);
  Multiplexer #(.width(32), .disabled(0), .enable("false")) multiplexer_25 (
    .in0(_25), .in1(or_71_out), .out(row_25_2), .sel(or_86_out));
  or or_87 (or_87_out, comparator_25_gt, comparator_25_eq);
  Multiplexer #(.width(32), .disabled(0), .enable("false")) multiplexer_26 (
    .in0(_26), .in1(or_72_out), .out(row_26_2), .sel(or_87_out));
  or or_88 (or_88_out, comparator_26_gt, comparator_26_eq);
  Multiplexer #(.width(32), .disabled(0), .enable("false")) multiplexer_27 (
    .in0(_27), .in1(or_73_out), .out(row_27_2), .sel(or_88_out));
  or or_89 (or_89_out, comparator_27_gt, comparator_27_eq);
  Multiplexer #(.width(32), .disabled(0), .enable("false")) multiplexer_28 (
    .in0(_28), .in1(or_74_out), .out(row_28_2), .sel(or_89_out));
  or or_90 (or_90_out, comparator_28_gt, comparator_28_eq);
  Multiplexer #(.width(32), .disabled(0), .enable("false")) multiplexer_29 (
    .in0(_29), .in1(or_75_out), .out(row_29_2), .sel(or_90_out));
  or or_91 (or_91_out, comparator_29_gt, comparator_29_eq);
  Multiplexer #(.width(32), .disabled(0), .enable("false")) multiplexer_30 (
    .in0(_30), .in1(or_76_out), .out(row_30_2), .sel(or_91_out));
  or or_92 (or_92_out, comparator_30_gt, comparator_30_eq);
  Multiplexer #(.width(32), .disabled(0), .enable("false")) multiplexer_31 (
    .in0(_31), .in1(or_77_out), .out(row_31_2), .sel(or_92_out));

  // Other names for the same wires on the sheet: _15[31:0] = row_15_2; _16[31:0] = row_16_2; row0[31:0] = row_0;
  //   row1[31:0] = row_1; row2[31:0] = row_2; row3[31:0] = row_3; row4[31:0] = row_4; row5[31:0] = row_5;
  //   row6[31:0] = row_6; row7[31:0] = row_7; row8[31:0] = row_8; row9[31:0] = row_9; row10[31:0] = row_10;
  //   row11[31:0] = row_11; row12[31:0] = row_12; row13[31:0] = row_13; row14[31:0] = row_14; row15[31:0] = row_15;
  //   row16[31:0] = row_16; row17[31:0] = row_17; row18[31:0] = row_18; row19[31:0] = row_19; row20[31:0] = row_20;
  //   row21[31:0] = row_21; row22[31:0] = row_22; row23[31:0] = row_23; row24[31:0] = row_24; row25[31:0] = row_25;
  //   row26[31:0] = row_26; row27[31:0] = row_27; row28[31:0] = row_28; row29[31:0] = row_29; row30[31:0] = row_30;
  //   row31[31:0] = row_31
endmodule

module neghbors (
  input  [4:0] Y,
  input  [31:0] row_0,
  input  [31:0] row_1,
  input  [31:0] row_2,
  input  [31:0] row_3,
  input  [31:0] row_4,
  input  [31:0] row_5,
  input  [31:0] row_6,
  input  [31:0] row_7,
  input  [31:0] row_8,
  input  [31:0] row_9,
  input  [31:0] row_10,
  input  [31:0] row_11,
  input  [4:0] X,
  input  [31:0] row_12,
  input  [31:0] row_13,
  input  [31:0] row_14,
  input  [31:0] row_15,
  input  [31:0] row_16,
  input  [31:0] row_17,
  input  [31:0] row_18,
  input  [31:0] row_19,
  input  [31:0] row_20,
  input  [31:0] row_21,
  input  [31:0] row_22,
  input  [31:0] row_23,
  input  [31:0] row_24,
  input  [31:0] row_25,
  input  [31:0] row_26,
  input  [31:0] row_27,
  input  [31:0] row_28,
  input  [31:0] row_29,
  input  [31:0] row_30,
  input  [31:0] row_31,
  output row_is_null,
  output bit_state,
  output [7:0] count_of_neghbors
);

  wire bit_state_1_bit_state, bit_state_2_bit_state, bit_state_3_bit_state, bit_state_4_bit_state,
       bit_state_6_bit_state, bit_state_7_bit_state, bit_state_8_bit_state, bit_state_9_bit_state,
       comparator_1_eq, comparator_2_eq, comparator_3_eq;
  wire [4:0] adder_1_out, adder_2_out, subtractor_1_out, subtractor_2_out;
  wire [7:0] adder_3_out, adder_4_out, adder_5_out, adder_6_out, adder_7_out, adder_8_out, adder_9_out,
       adder_10_out;
  wire [31:0] multiplexer_1_out, multiplexer_2_out, multiplexer_3_out;

  Subtractor #(.width(5)) subtractor_1 (.a(Y), .b(5'b00001), .out(subtractor_1_out));  // open: bin, bout
  Multiplexer #(.select(5), .width(32), .disabled(0), .enable("false")) multiplexer_1 (
    .in0(row_0), .in1(row_1), .in2(row_2), .in3(row_3), .in4(row_4), .in5(row_5), .in6(row_6), .in7(row_7),
    .in8(row_8), .in9(row_9), .in10(row_10), .in11(row_11), .in12(row_12), .in13(row_13), .in14(row_14),
    .in15(row_15), .in16(row_16), .in17(row_17), .in18(row_18), .in19(row_19), .in20(row_20), .in21(row_21),
    .in22(row_22), .in23(row_23), .in24(row_24), .in25(row_25), .in26(row_26), .in27(row_27), .in28(row_28),
    .in29(row_29), .in30(row_30), .in31(row_31), .out(multiplexer_1_out), .sel(subtractor_1_out));
  Adder #(.width(5)) adder_1 (.a(X), .b(5'b00001), .out(adder_1_out));  // open: cin, cout
  Subtractor #(.width(5)) subtractor_2 (.a(X), .b(5'b00001), .out(subtractor_2_out));  // open: bin, bout
  Multiplexer #(.select(5), .width(32), .disabled(0), .enable("false")) multiplexer_2 (
    .in0(row_0), .in1(row_1), .in2(row_2), .in3(row_3), .in4(row_4), .in5(row_5), .in6(row_6), .in7(row_7),
    .in8(row_8), .in9(row_9), .in10(row_10), .in11(row_11), .in12(row_12), .in13(row_13), .in14(row_14),
    .in15(row_15), .in16(row_16), .in17(row_17), .in18(row_18), .in19(row_19), .in20(row_20), .in21(row_21),
    .in22(row_22), .in23(row_23), .in24(row_24), .in25(row_25), .in26(row_26), .in27(row_27), .in28(row_28),
    .in29(row_29), .in30(row_30), .in31(row_31), .out(multiplexer_2_out), .sel(Y));
  Adder #(.width(5)) adder_2 (.a(Y), .b(5'b00001), .out(adder_2_out));  // open: cin, cout
  Multiplexer #(.select(5), .width(32), .disabled(0), .enable("false")) multiplexer_3 (
    .in0(row_0), .in1(row_1), .in2(row_2), .in3(row_3), .in4(row_4), .in5(row_5), .in6(row_6), .in7(row_7),
    .in8(row_8), .in9(row_9), .in10(row_10), .in11(row_11), .in12(row_12), .in13(row_13), .in14(row_14),
    .in15(row_15), .in16(row_16), .in17(row_17), .in18(row_18), .in19(row_19), .in20(row_20), .in21(row_21),
    .in22(row_22), .in23(row_23), .in24(row_24), .in25(row_25), .in26(row_26), .in27(row_27), .in28(row_28),
    .in29(row_29), .in30(row_30), .in31(row_31), .out(multiplexer_3_out), .sel(adder_2_out));
  bit_state bit_state_1 (.bit_state(bit_state_1_bit_state), .X(adder_1_out), .Y(multiplexer_1_out));
  bit_state bit_state_2 (.bit_state(bit_state_2_bit_state), .X(X), .Y(multiplexer_1_out));
  bit_state bit_state_3 (.bit_state(bit_state_3_bit_state), .X(subtractor_2_out), .Y(multiplexer_1_out));
  bit_state bit_state_4 (.bit_state(bit_state_4_bit_state), .X(adder_1_out), .Y(multiplexer_2_out));
  bit_state bit_state_5 (.bit_state(bit_state), .X(X), .Y(multiplexer_2_out));
  bit_state bit_state_6 (.bit_state(bit_state_6_bit_state), .X(subtractor_2_out), .Y(multiplexer_2_out));
  bit_state bit_state_7 (.bit_state(bit_state_7_bit_state), .X(adder_1_out), .Y(multiplexer_3_out));
  bit_state bit_state_8 (.bit_state(bit_state_8_bit_state), .X(X), .Y(multiplexer_3_out));
  bit_state bit_state_9 (.bit_state(bit_state_9_bit_state), .X(subtractor_2_out), .Y(multiplexer_3_out));
  Comparator #(.width(32)) comparator_1 (.a(multiplexer_3_out), .b({32{1'b0}}), .eq(comparator_1_eq));  // open: gt, lt
  Comparator #(.width(32)) comparator_2 (.a(multiplexer_2_out), .b({32{1'b0}}), .eq(comparator_2_eq));  // open: gt, lt
  Comparator #(.width(32)) comparator_3 (.a(multiplexer_1_out), .b({32{1'b0}}), .eq(comparator_3_eq));  // open: gt, lt
  and and_1 (row_is_null, comparator_1_eq, comparator_2_eq, comparator_3_eq);
  Adder adder_3 (.a({8{1'b0}}), .b({8{1'b0}}), .out(adder_3_out), .cin(bit_state_1_bit_state));  // open: cout
  Adder adder_4 (.a(adder_3_out), .b({8{1'b0}}), .out(adder_4_out), .cin(bit_state_2_bit_state));  // open: cout
  Adder adder_5 (.a({8{1'b0}}), .b(adder_6_out), .out(adder_5_out), .cin(bit_state_8_bit_state));  // open: cout
  Adder adder_6 (.a({8{1'b0}}), .b({8{1'b0}}), .out(adder_6_out), .cin(bit_state_9_bit_state));  // open: cout
  Adder adder_7 (.a(adder_4_out), .b({8{1'b0}}), .out(adder_7_out), .cin(bit_state_3_bit_state));  // open: cout
  Adder adder_8 (.a(adder_7_out), .b({8{1'b0}}), .out(adder_8_out), .cin(bit_state_4_bit_state));  // open: cout
  Adder adder_9 (.a({8{1'b0}}), .b(adder_10_out), .out(adder_9_out), .cin(bit_state_6_bit_state));  // open: cout
  Adder adder_10 (.a({8{1'b0}}), .b(adder_5_out), .out(adder_10_out), .cin(bit_state_7_bit_state));  // open: cout
  Adder adder_11 (.a(adder_8_out), .b(adder_9_out), .out(count_of_neghbors));  // open: cin, cout

  // Other names for the same wires on the sheet: row0[31:0] = row_0; row1[31:0] = row_1; row2[31:0] = row_2;
  //   row3[31:0] = row_3; row4[31:0] = row_4; row5[31:0] = row_5; row6[31:0] = row_6; row7[31:0] = row_7;
  //   row8[31:0] = row_8; row9[31:0] = row_9; row10[31:0] = row_10; row11[31:0] = row_11; row12[31:0] = row_12;
  //   row13[31:0] = row_13; row14[31:0] = row_14; row15[31:0] = row_15; row16[31:0] = row_16; row17[31:0] = row_17;
  //   row18[31:0] = row_18; row19[31:0] = row_19; row20[31:0] = row_20; row21[31:0] = row_21; row22[31:0] = row_22;
  //   row23[31:0] = row_23; row24[31:0] = row_24; row25[31:0] = row_25; row26[31:0] = row_26; row27[31:0] = row_27;
  //   row28[31:0] = row_28; row29[31:0] = row_29; row30[31:0] = row_30; row31[31:0] = row_31

  // Notes on the sheet:
  //   Y - 1
  //   Y 
  //   Y + 1
endmodule

module bit_state (
  input  [4:0] X,
  input  [31:0] Y,
  output bit_state
);

  wire [31:0] and_1_out, decoder_1_out0;

  Decoder #(.select(5), .disabled(0), .enable("false")) decoder_1 (
    .out0(decoder_1_out0[0]), .out1(decoder_1_out0[1]), .out2(decoder_1_out0[2]), .out3(decoder_1_out0[3]),
    .out4(decoder_1_out0[4]), .out5(decoder_1_out0[5]), .out6(decoder_1_out0[6]), .out7(decoder_1_out0[7]),
    .out8(decoder_1_out0[8]), .out9(decoder_1_out0[9]), .out10(decoder_1_out0[10]),
    .out11(decoder_1_out0[11]), .out12(decoder_1_out0[12]), .out13(decoder_1_out0[13]),
    .out14(decoder_1_out0[14]), .out15(decoder_1_out0[15]), .out16(decoder_1_out0[16]),
    .out17(decoder_1_out0[17]), .out18(decoder_1_out0[18]), .out19(decoder_1_out0[19]),
    .out20(decoder_1_out0[20]), .out21(decoder_1_out0[21]), .out22(decoder_1_out0[22]),
    .out23(decoder_1_out0[23]), .out24(decoder_1_out0[24]), .out25(decoder_1_out0[25]),
    .out26(decoder_1_out0[26]), .out27(decoder_1_out0[27]), .out28(decoder_1_out0[28]),
    .out29(decoder_1_out0[29]), .out30(decoder_1_out0[30]), .out31(decoder_1_out0[31]), .sel(X));
  assign and_1_out = Y & decoder_1_out0;  // AND_Gate and_1, 32 bits wide
  or or_1 (bit_state, and_1_out[0], and_1_out[1], and_1_out[2], and_1_out[3], and_1_out[4], and_1_out[5], and_1_out[6], and_1_out[7], and_1_out[8], and_1_out[9], and_1_out[10], and_1_out[11], and_1_out[12], and_1_out[13], and_1_out[14], and_1_out[15], and_1_out[16], and_1_out[17], and_1_out[18], and_1_out[19], and_1_out[20], and_1_out[21], and_1_out[22], and_1_out[23], and_1_out[24], and_1_out[25], and_1_out[26], and_1_out[27], and_1_out[28], and_1_out[29], and_1_out[30], and_1_out[31]);
endmodule

module survival (
  input  [31:0] row_0,
  input  [31:0] row_1,
  input  [31:0] row_2,
  input  [31:0] row_3,
  input  [31:0] row_4,
  input  [31:0] row_5,
  input  [31:0] row_6,
  input  [31:0] row_7,
  input  [31:0] row_8,
  input  [31:0] row_9,
  input  [31:0] row_10,
  input  [31:0] row_11,
  input  [31:0] row_12,
  input  [31:0] row_13,
  input  [31:0] row_14,
  input  [31:0] row_15,
  input  [31:0] row_16,
  input  [31:0] row_17,
  input  [31:0] row_18,
  input  [31:0] row_19,
  input  [31:0] row_20,
  input  [31:0] row_21,
  input  [31:0] row_22,
  input  [31:0] row_23,
  input  [31:0] row_24,
  input  [31:0] row_25,
  input  [31:0] row_26,
  input  [31:0] row_27,
  input  [31:0] row_28,
  input  [31:0] row_29,
  input  [31:0] row_30,
  input  [31:0] row_31,
  output no_any_alive,
  output WIN_1__or_LOSE_0
);

  wire [31:0] or_1_out;

  assign or_1_out = row_0 | row_1 | row_2 | row_3 | row_4 | row_5 | row_6 | row_7 | row_8 | row_9 | row_10 | row_11 | row_12 | row_13 | row_14 | row_15 | row_16 | row_17 | row_18 | row_19 | row_20 | row_21 | row_22 | row_23 | row_24 | row_25 | row_26 | row_27 | row_28 | row_29 | row_30 | row_31;  // OR_Gate or_1, 32 bits wide
  or or_2 (WIN_1__or_LOSE_0, or_1_out[0], or_1_out[1], or_1_out[2], or_1_out[3], or_1_out[4], or_1_out[5], or_1_out[6], or_1_out[7], or_1_out[8], or_1_out[9], or_1_out[10], or_1_out[11], or_1_out[12], or_1_out[13], or_1_out[14], or_1_out[15], or_1_out[17], or_1_out[18], or_1_out[19], or_1_out[20], or_1_out[21], or_1_out[22], or_1_out[23], or_1_out[24], or_1_out[25], or_1_out[26], or_1_out[27], or_1_out[28], or_1_out[29], or_1_out[30], or_1_out[31], or_1_out[16]);
  not not_1 (no_any_alive, WIN_1__or_LOSE_0);

  // Other names for the same wires on the sheet: row0[31:0] = row_0; row1[31:0] = row_1; row2[31:0] = row_2;
  //   row3[31:0] = row_3; row4[31:0] = row_4; row5[31:0] = row_5; row6[31:0] = row_6; row7[31:0] = row_7;
  //   row8[31:0] = row_8; row9[31:0] = row_9; row10[31:0] = row_10; row11[31:0] = row_11; row12[31:0] = row_12;
  //   row13[31:0] = row_13; row14[31:0] = row_14; row15[31:0] = row_15; row16[31:0] = row_16; row17[31:0] = row_17;
  //   row18[31:0] = row_18; row19[31:0] = row_19; row20[31:0] = row_20; row21[31:0] = row_21; row22[31:0] = row_22;
  //   row23[31:0] = row_23; row24[31:0] = row_24; row25[31:0] = row_25; row26[31:0] = row_26; row27[31:0] = row_27;
  //   row28[31:0] = row_28; row29[31:0] = row_29; row30[31:0] = row_30; row31[31:0] = row_31
endmodule

module status_bar (
  input  game_ON___OFF,
  input  creative___survival,
  input  WIN___LOSE,
  input  [9:0] cursor,
  input  show_result,
  output [31:0] out_6,
  output [31:0] out_7,
  output [31:0] out_8,
  output clear_field,
  output [31:0] out_10,
  output [31:0] out_11,
  output [31:0] out_12,
  output [31:0] out_13
);

  wire comparator_1_gt, comparator_1_lt, movement, not_1_out, not_2_out, not_3_out, not_4_out, not_5_out,
       not_6_out, not_7_out, show_res, xor_1_out;
  wire [3:0] show;
  wire [9:0] register_2_q;

  Register #(.width(1)) register_1 (.D(show_result), .Q(show_res), .clk(not_1_out), .clr(movement));  // open: en
  not not_1 (not_1_out, not_2_out);
  not not_2 (not_2_out, show_result);
  Register #(.width(10)) register_2 (.D(cursor), .Q(register_2_q), .clk(game_ON___OFF));  // open: en, clr
  Comparator #(.width(10)) comparator_1 (
    .a(cursor), .b(register_2_q), .gt(comparator_1_gt), .lt(comparator_1_lt));  // open: eq
  or or_1 (movement, comparator_1_gt, comparator_1_lt);
  not not_3 (not_3_out, game_ON___OFF);
  not not_4 (not_4_out, game_ON___OFF);
  not not_5 (not_5_out, WIN___LOSE);
  not not_6 (not_6_out, movement);
  and and_1 (show[0], ~game_ON___OFF, ~show_res);  // AND_Gate
  and and_2 (show[2], show_res, not_3_out, creative___survival, WIN___LOSE);
  and and_3 (show[3], show_res, not_4_out, creative___survival, not_5_out);
  not not_7 (not_7_out, xor_1_out);
  xor xor_1 (xor_1_out, not_6_out, movement);
  and and_4 (clear_field, not_7_out, show_res);
  Multiplexer #(.select(4), .width(32), .disabled(0), .enable("false")) multiplexer_1 (
    .in0(32'h3dcef80), .in1(32'h3dcef80), .in2(32'h6aaa5d75), .in4(32'h45d100), .in8(32'h10c7780),
    .out(out_7), .sel({show[3:2], game_ON___OFF, show[0]}));  // open: in3, in5, in6, in7, in9, in10, in11, in12, in13, in14, in15
  Multiplexer #(.select(4), .width(32), .disabled(0), .enable("false")) multiplexer_2 (
    .in0(32'h2124200), .in1(32'h2124200), .in2(32'h8baaa955), .in4(32'h449900), .in8(32'h1128400),
    .out(out_8), .sel({show[3:2], game_ON___OFF, show[0]}));  // open: in3, in5, in6, in7, in9, in10, in11, in12, in13, in14, in15
  Multiplexer #(.select(4), .width(32), .disabled(0), .enable("false")) multiplexer_3 (
    .in0(32'h3924200), .in1(32'h3924200), .in2(32'h4aaae955), .in4(32'h549500), .in8(32'h1126700),
    .out(out_10), .sel({show[3:2], game_ON___OFF, show[0]}));  // open: in3, in5, in6, in7, in9, in10, in11, in12, in13, in14, in15
  Multiplexer #(.select(4), .width(32), .disabled(0), .enable("false")) multiplexer_4 (
    .in0(32'h2124200), .in1(32'h2124200), .in2(32'h2aaaa957), .in4(32'h6c9300), .in8(32'h1121400),
    .out(out_11), .sel({show[3:2], game_ON___OFF, show[0]}));  // open: in3, in5, in6, in7, in9, in10, in11, in12, in13, in14, in15
  Multiplexer #(.select(4), .width(32), .disabled(0), .enable("false")) multiplexer_5 (
    .in0(32'h3dce200), .in1(32'h3dce200), .in2(32'hca93a975), .in4(32'h45d100), .in8(32'h1cce780),
    .out(out_12), .sel({show[3:2], game_ON___OFF, show[0]}));  // open: in3, in5, in6, in7, in9, in10, in11, in12, in13, in14, in15

  assign out_6 = {32{1'b0}};
  assign out_13 = {32{1'b0}};

  // Other names for the same wires on the sheet: creat___sur = creative___survival; show[1] = game_ON___OFF;
  //   W___L = WIN___LOSE
endmodule

module GAME (
  input  [7:0] _87654321,
  input  [7:0] _0,
  input  _87654321_2,
  input  in_4,
  input  [3:0] Zone_width
);

  wire button_2_out, button_3_out, button_4_out, button_out, main_1_clock, main_1_out_26, not_1_out,
       patterns_1_out_4, patterns_1_out_5, patterns_1_out_6, patterns_1_out_7, patterns_1_out_8,
       patterns_1_out_9, patterns_1_out_10;
  wire [2:0] patterns_1_out_3;
  wire [6:0] keyboard_1_data;
  wire [31:0] main_1_row_0, main_1_row_1, main_1_row_2, main_1_row_3, main_1_row_4, main_1_row_5,
       main_1_row_6, main_1_row_7, main_1_row_8, main_1_row_9, main_1_row_10, main_1_row_11, main_1_row_12,
       main_1_row_13, main_1_row_14, main_1_row_15, main_1_row_16, main_1_row_17, main_1_row_18,
       main_1_row_19, main_1_row_20, main_1_row_21, main_1_row_22, main_1_row_23, main_1_row_24,
       main_1_row_25, main_1_row_26, main_1_row_27, main_1_row_28, main_1_row_29, main_1_row_30,
       main_1_row_31, main_1_stb_0, main_1_stb_1, main_1_stb_2, main_1_stb_3, main_1_stb_4, main_1_stb_5,
       main_1_stb_6;

  _7_Segment_Display u_7_segment_display_1 (
    .g(patterns_1_out_4), .f(patterns_1_out_5), .a(patterns_1_out_6), .b(patterns_1_out_7),
    .e(patterns_1_out_8), .d(patterns_1_out_9), .c(patterns_1_out_10));  // open: dp
  patterns patterns_1 (
    .in_1(button_out), .in_2(button_2_out), .out_3(patterns_1_out_3), .out_8(patterns_1_out_8),
    .out_9(patterns_1_out_9), .out_10(patterns_1_out_10), .out_7(patterns_1_out_7), .out_6(patterns_1_out_6),
    .out_5(patterns_1_out_5), .out_4(patterns_1_out_4));
  Button button (.out(button_out));
  Button button_2 (.out(button_2_out));
  DotMatrix #(.inputtype("row"), .matrixcols(32)) dotmatrix_1 (
    .row0(main_1_stb_0), .row1(main_1_stb_1), .row2(main_1_stb_2), .row3(main_1_stb_3), .row4(main_1_stb_4),
    .row5(main_1_stb_5), .row6(main_1_stb_6));
  DotMatrix #(.inputtype("row"), .matrixcols(32), .matrixrows(32)) dotmatrix_2 (
    .row0(main_1_row_0), .row1(main_1_row_1), .row2(main_1_row_2), .row3(main_1_row_3), .row4(main_1_row_4),
    .row5(main_1_row_5), .row6(main_1_row_6), .row7(main_1_row_7), .row8(main_1_row_8), .row9(main_1_row_9),
    .row10(main_1_row_10), .row11(main_1_row_11), .row12(main_1_row_12), .row13(main_1_row_13),
    .row14(main_1_row_14), .row15(main_1_row_15), .row16(main_1_row_16), .row17(main_1_row_17),
    .row18(main_1_row_18), .row19(main_1_row_19), .row20(main_1_row_20), .row21(main_1_row_21),
    .row22(main_1_row_22), .row23(main_1_row_23), .row24(main_1_row_24), .row25(main_1_row_25),
    .row26(main_1_row_26), .row27(main_1_row_27), .row28(main_1_row_28), .row29(main_1_row_29),
    .row30(main_1_row_30), .row31(main_1_row_31));
  Button button_3 (.out(button_3_out));
  Keyboard keyboard_1 (.clk(main_1_clock), .re(main_1_out_26), .clr(not_1_out), .data(keyboard_1_data));  // open: avail
  not not_1 (not_1_out, main_1_out_26);
  Button button_4 (.out(button_4_out));
  main main_1 (
    .birth(_87654321), .survival(_0), .creative__0____survival__1(in_4), .game_ON___OFF(button_3_out),
    .clear_field(button_4_out), .clock(main_1_clock), .row_0(main_1_row_0), .row_1(main_1_row_1),
    .row_2(main_1_row_2), .row_3(main_1_row_3), .row_4(main_1_row_4), .row_5(main_1_row_5),
    .row_6(main_1_row_6), .row_7(main_1_row_7), .row_8(main_1_row_8), .row_9(main_1_row_9),
    .row_10(main_1_row_10), .row_11(main_1_row_11), .row_12(main_1_row_12), .row_13(main_1_row_13),
    .row_14(main_1_row_14), .row_15(main_1_row_15), .row_16(main_1_row_16), .row_17(main_1_row_17),
    .row_18(main_1_row_18), .row_19(main_1_row_19), .row_20(main_1_row_20), .row_21(main_1_row_21),
    .row_22(main_1_row_22), .row_23(main_1_row_23), .row_24(main_1_row_24), .row_25(main_1_row_25),
    .row_26(main_1_row_26), .row_27(main_1_row_27), .row_28(main_1_row_28), .row_29(main_1_row_29),
    .row_30(main_1_row_30), .row_31(main_1_row_31), .stb_0(main_1_stb_0), .stb_1(main_1_stb_1),
    .stb_2(main_1_stb_2), .stb_3(main_1_stb_3), .stb_4(main_1_stb_4), .stb_5(main_1_stb_5),
    .stb_6(main_1_stb_6), .cursor(keyboard_1_data), .out_26(main_1_out_26), .zone_width(Zone_width),
    .survival_cond__if_null(_87654321_2), .ID_of_pattern(patterns_1_out_3));

  // Notes on the sheet:
  //   Birth condition
  //   ON/OFF
  //   Creative(0) / Survival(1)
  //   Survival condition
  //   Clear
  //   Cursor
  //   0-15
endmodule

module \wait  (
  input  in_1,
  output out_2
);

  wire not_1_out, not_2_out, not_3_out, not_4_out, not_5_out, not_6_out, not_7_out, not_8_out, not_10_out;

  not not_1 (not_1_out, not_2_out);
  not not_2 (not_2_out, not_3_out);
  not not_3 (not_3_out, in_1);
  not not_4 (not_4_out, not_1_out);
  not not_5 (not_5_out, not_4_out);
  not not_6 (not_6_out, not_7_out);
  not not_7 (not_7_out, not_5_out);
  not not_8 (not_8_out, not_6_out);
  not not_9 (out_2, not_10_out);
  not not_10 (not_10_out, not_8_out);
endmodule

module patterns (
  input  in_1,
  input  in_2,
  output [2:0] out_3,
  output out_4,
  output out_5,
  output out_6,
  output out_7,
  output out_8,
  output out_9,
  output out_10
);

  wire or_1_out;

  Counter #(.width(3), .max('h7)) counter_1 (.load(in_2), .Q(out_3), .clk(or_1_out));  // open: D, count, carry, clr
  or or_1 (or_1_out, in_2, in_1);
  Multiplexer #(.select(3), .width(7), .enable("false")) multiplexer_1 (
    .in0(7'b0111111), .in1(7'b0001100), .in2(7'b1011011), .in3(7'b1011110), .in4(7'b1101100),
    .in5(7'b1110110), .in6(7'b1110111), .in7(7'b0011100),
    .out({out_4, out_5, out_6, out_7, out_10, out_9, out_8}), .sel(out_3));
endmodule
